// Logisim project Trabalho2_final.circ as structural Verilog: 12 circuits, main circuit mux
module main (
  input  Reset
);

  wire Botao_Pedestre_out, clock_1_out, decodificador_p_1_verde, decodificador_p_1_vermelho,
       decodificador_p_2_verde, decodificador_p_2_vermelho, decodificador_s1_1_amarela,
       decodificador_s1_1_verde, decodificador_s1_1_vermelha, decodificador_s2_1_amarela,
       decodificador_s2_1_verde, decodificador_s2_1_vermelha, decodificador_s3_1_amarela,
       decodificador_s3_1_verde, decodificador_s3_1_vermelha, filpflop_sr_1_q, flipflop_d_1_q,
       flipflop_d_2_q, flipflop_d_3_q, flipflop_d_4_q, mux_1_saida, mux_2_saida, mux_3_saida, mux_4_saida,
       p0_1_f0, p1_1_f1, p2_1_f2, p3_1_f3;

  Button Botao_Pedestre (.out(Botao_Pedestre_out));
  FilpFlop_SR filpflop_sr_1 (
    .S(Botao_Pedestre_out), .Clk(clock_1_out), .R(decodificador_p_1_verde), .Q(filpflop_sr_1_q));  // open: Qn
  decodificador_S1 decodificador_s1_1 (
    .B3(flipflop_d_4_q), .B2(flipflop_d_3_q), .B1(flipflop_d_2_q), .B0(flipflop_d_1_q),
    .verde(decodificador_s1_1_verde), .amarela(decodificador_s1_1_amarela),
    .vermelha(decodificador_s1_1_vermelha));
  LED led_1 (.in(decodificador_p_1_verde));
  LED led_2 (.in(decodificador_p_1_vermelho));
  LED led_3 (.in(decodificador_p_1_verde));
  LED led_4 (.in(decodificador_p_1_vermelho));
  decodificador_P decodificador_p_1 (
    .B3(flipflop_d_4_q), .B2(flipflop_d_3_q), .B1(flipflop_d_2_q), .verde(decodificador_p_1_verde),
    .vermelho(decodificador_p_1_vermelho));
  P0 p0_1 (
    .Entrada(filpflop_sr_1_q), .B3(flipflop_d_4_q), .B2(flipflop_d_3_q), .B1(flipflop_d_2_q),
    .B0(flipflop_d_1_q), .f0(p0_1_f0));
  P1 p1_1 (.Entrada(filpflop_sr_1_q), .B2(flipflop_d_3_q), .B1(flipflop_d_2_q), .B0(flipflop_d_1_q), .f1(p1_1_f1));
  P2 p2_1 (.Entrada(filpflop_sr_1_q), .B2(flipflop_d_3_q), .B1(flipflop_d_2_q), .B0(flipflop_d_1_q), .f2(p2_1_f2));
  P3 p3_1 (.Entrada(filpflop_sr_1_q), .B2(flipflop_d_3_q), .B1(flipflop_d_2_q), .B0(flipflop_d_1_q), .f3(p3_1_f3));
  LED led_5 (.in(decodificador_s1_1_vermelha));
  LED led_6 (.in(decodificador_s1_1_amarela));
  LED led_7 (.in(decodificador_s1_1_verde));
  LED led_8 (.in(decodificador_s2_1_vermelha));
  LED led_9 (.in(decodificador_s2_1_amarela));
  decodificador_S2 decodificador_s2_1 (
    .B3(flipflop_d_4_q), .B2(flipflop_d_3_q), .B1(flipflop_d_2_q), .B0(flipflop_d_1_q),
    .verde(decodificador_s2_1_verde), .amarela(decodificador_s2_1_amarela),
    .vermelha(decodificador_s2_1_vermelha));
  LED led_10 (.in(decodificador_s2_1_verde));
  mux mux_1 (.A(1'b0), .B(p0_1_f0), .Sel(Reset), .saida(mux_1_saida));
  mux mux_2 (.A(1'b0), .B(p1_1_f1), .Sel(Reset), .saida(mux_2_saida));
  mux mux_3 (.A(1'b0), .B(p2_1_f2), .Sel(Reset), .saida(mux_3_saida));
  mux mux_4 (.A(1'b0), .B(p3_1_f3), .Sel(Reset), .saida(mux_4_saida));
  LED led_11 (.in(decodificador_p_2_verde));
  LED led_12 (.in(decodificador_p_2_vermelho));
  LED led_13 (.in(decodificador_s3_1_verde));
  LED led_14 (.in(decodificador_s3_1_amarela));
  LED led_15 (.in(decodificador_s3_1_vermelha));
  LED led_16 (.in(decodificador_p_2_verde));
  LED led_17 (.in(decodificador_p_2_vermelho));
  Clock clock_1 (.out(clock_1_out));
  decodificador_P decodificador_p_2 (
    .B3(flipflop_d_4_q), .B2(flipflop_d_3_q), .B1(flipflop_d_2_q), .verde(decodificador_p_2_verde),
    .vermelho(decodificador_p_2_vermelho));
  decodificador_S3 decodificador_s3_1 (
    .B3(flipflop_d_4_q), .B2(flipflop_d_3_q), .B1(flipflop_d_2_q), .B0(flipflop_d_1_q),
    .verde(decodificador_s3_1_verde), .amarela(decodificador_s3_1_amarela),
    .vermelha(decodificador_s3_1_vermelha));
  FlipFlop_D flipflop_d_1 (.D(mux_1_saida), .Clk(clock_1_out), .Q(flipflop_d_1_q));  // open: Qn
  FlipFlop_D flipflop_d_2 (.D(mux_2_saida), .Clk(clock_1_out), .Q(flipflop_d_2_q));  // open: Qn
  FlipFlop_D flipflop_d_3 (.D(mux_3_saida), .Clk(clock_1_out), .Q(flipflop_d_3_q));  // open: Qn
  FlipFlop_D flipflop_d_4 (.D(mux_4_saida), .Clk(clock_1_out), .Q(flipflop_d_4_q));  // open: Qn

  // Notes on the sheet:
  //   Para iniciar o circuito, acione a entrada reset e precione o Botao_Pedestre
  //   Apos isso desligue a entrada reset
  //   FlipFlop que registra o aperto do botao para o pedestre
  //   bits P0 P1 P2 P3
  //   que representam o proximo estado do circuito
  //   Mux presente para reiniciar o circuito
  //   B0
  //   B1
  //   B2
  //   B3
  //   FlipFlops do tipo D ou componentes de memoria, 
  //   que registram os bits estado atual e enviam uma saida para o circuito
  //   ao mesmo tempo em que enviam dados para os proximo estado
  //   decodificadores que tranformam os bits B0 B1 B2 B3
  //   em saidas para os semaforos S1 S2 S3 e Pedestres
endmodule

module mux (
  input  A,
  input  B,
  input  Sel,
  output saida
);

  wire and_1_out, and_2_out, not_1_out;

  and and_1 (and_1_out, A, Sel);
  and and_2 (and_2_out, B, not_1_out);
  not not_1 (not_1_out, Sel);
  or or_1 (saida, and_1_out, and_2_out);
endmodule

module P0 (
  input  Entrada,
  input  B3,
  input  B2,
  input  B1,
  input  B0,
  output f0
);

  wire and_1_out, and_2_out, and_3_out;

  and and_1 (and_1_out, ~B0, ~B1, ~B3);  // AND_Gate
  and and_2 (and_2_out, ~B0, B1, ~B2);  // AND_Gate
  and and_3 (and_3_out, Entrada, B1, B2);
  or or_1 (f0, and_1_out, and_2_out, and_3_out);
endmodule

module P1 (
  input  Entrada,
  input  B2,
  input  B1,
  input  B0,
  output f1
);

  wire and_1_out, and_2_out, and_3_out, and_4_out;

  and and_1 (and_1_out, B0, ~B1, ~B2);  // AND_Gate
  and and_2 (and_2_out, ~B0, B1, ~B2);  // AND_Gate
  and and_3 (and_3_out, Entrada, B0, ~B2);  // AND_Gate
  and and_4 (and_4_out, Entrada, B1, ~B2);  // AND_Gate
  or or_1 (f1, and_1_out, and_2_out, and_3_out, and_4_out);
endmodule

module P2 (
  input  Entrada,
  input  B2,
  input  B1,
  input  B0,
  output f2
);

  wire and_1_out, and_2_out, and_3_out;

  and and_1 (and_1_out, ~B0, ~B1, B2);  // AND_Gate
  and and_2 (and_2_out, B0, B1, ~B2);  // AND_Gate
  and and_3 (and_3_out, Entrada, B0, ~B1);  // AND_Gate
  or or_1 (f2, and_1_out, and_2_out, and_3_out);
endmodule

module P3 (
  input  Entrada,
  input  B2,
  input  B1,
  input  B0,
  output f3
);

  and and_1 (f3, Entrada, B0, ~B1, B2);  // AND_Gate
endmodule

module FlipFlop_D (
  input  D,
  input  Clk,
  output Q,
  output Qn
);

  wire nand_1_out, nand_2_out, nand_3_out, nand_4_out, nand_5_out, nand_6_out, not_1_out, not_2_out;

  not not_1 (not_1_out, D);
  nand nand_1 (nand_1_out, D, Clk);
  nand nand_2 (nand_2_out, Clk, not_1_out);
  nand nand_3 (nand_3_out, nand_1_out, nand_4_out);
  nand nand_4 (nand_4_out, nand_3_out, nand_2_out);
  not not_2 (not_2_out, Clk);
  nand nand_5 (nand_5_out, nand_3_out, not_2_out);
  nand nand_6 (nand_6_out, not_2_out, nand_4_out);
  nand nand_7 (Q, nand_5_out, Qn);
  nand nand_8 (Qn, Q, nand_6_out);
endmodule

module decodificador_S3 (
  input  B3,
  input  B2,
  input  B1,
  input  B0,
  output verde,
  output amarela,
  output vermelha
);

  and and_1 (verde, ~B0, ~B1, ~B2, ~B3);  // AND_Gate
  and and_2 (amarela, B0, ~B1, ~B2, ~B3);  // AND_Gate
  and and_3 (vermelha, ~amarela, ~verde);  // AND_Gate
endmodule

module decodificador_S2 (
  input  B3,
  input  B2,
  input  B1,
  input  B0,
  output verde,
  output amarela,
  output vermelha
);

  and and_1 (verde, ~B0, ~B1, B2, ~B3);  // AND_Gate
  and and_2 (amarela, B0, ~B1, B2, ~B3);  // AND_Gate
  and and_3 (vermelha, ~amarela, ~verde);  // AND_Gate
endmodule

module decodificador_S1 (
  input  B3,
  input  B2,
  input  B1,
  input  B0,
  output verde,
  output amarela,
  output vermelha
);

  and and_1 (verde, ~B0, B1, ~B2, ~B3);  // AND_Gate
  and and_2 (amarela, B0, B1, ~B2, ~B3);  // AND_Gate
  and and_3 (vermelha, ~amarela, ~verde);  // AND_Gate
endmodule

module decodificador_P (
  input  B3,
  input  B2,
  input  B1,
  output verde,
  output vermelho
);

  wire and_1_out;

  and and_1 (and_1_out, B1, B2);
  or or_1 (verde, B3, and_1_out);
  not not_1 (vermelho, verde);
endmodule

module FilpFlop_SR (
  input  S,
  input  Clk,
  input  R,
  output Q,
  output Qn
);

  wire nand_1_out, nand_2_out, nand_3_out, nand_4_out, nand_5_out, nand_6_out, not_1_out;

  nand nand_1 (nand_1_out, S, Clk);
  nand nand_2 (nand_2_out, Clk, R);
  nand nand_3 (nand_3_out, nand_1_out, nand_4_out);
  nand nand_4 (nand_4_out, nand_3_out, nand_2_out);
  not not_1 (not_1_out, Clk);
  nand nand_5 (nand_5_out, nand_3_out, not_1_out);
  nand nand_6 (nand_6_out, not_1_out, nand_4_out);
  nand nand_7 (Q, nand_5_out, Qn);
  nand nand_8 (Qn, Q, nand_6_out);
endmodule
