// Digital circuit Main-Ula.dig as structural Verilog
module Main_Ula (
  input  [15:0] A,
  input  [15:0] B,
  input  [2:0] F,
  output [15:0] R,
  output S0_Zero,
  output S1_OVFL,
  output S2_NEG
);

  wire Ovfl__1, Ovfl__plus_1, Ovfl_soma, OVFL_sub;
  wire [15:0] a_1_1_s, a_1_2_s, a_negado_1_s, a_xor_b_1_s, deslocador_direita_1_s, deslocador_esquerda_1_s,
       somador_completo16bits_1_s, subtracao_16bits_1_s;

  Deslocador_esquerda deslocador_esquerda_1 (.A(A), .B(B), .S(deslocador_esquerda_1_s));
  Deslocador_direita deslocador_direita_1 (.A(A), .B(B), .S(deslocador_direita_1_s));
  A_xor_B a_xor_b_1 (.A(A), .B(B), .S(a_xor_b_1_s));
  A_negado a_negado_1 (.A(A), .S(a_negado_1_s));
  somador_completo16bits somador_completo16bits_1 (.A(A), .B(B), .S(somador_completo16bits_1_s), .OVFL(Ovfl_soma));
  Subtracao_16bits subtracao_16bits_1 (.A(A), .B(B), .S(subtracao_16bits_1_s), .OVFL(OVFL_sub));
  A_1 a_1_1 (.A(A), .S(a_1_1_s), .OVFL(Ovfl__plus_1));
  A_1 a_1_2 (.A(A), .S(a_1_2_s), .OVFL(Ovfl__1));
  mux8x1 mux8x1_1 (
    ._0(deslocador_esquerda_1_s), ._1(deslocador_direita_1_s), ._2(a_xor_b_1_s), ._3(a_negado_1_s),
    ._4(somador_completo16bits_1_s), ._5(subtracao_16bits_1_s), ._6(a_1_1_s), ._7(a_1_2_s), .F(F), .S(R));
  mux8x1_1bit mux8x1_1bit_1 (
    ._0(1'b0), ._1(1'b0), ._2(1'b0), ._3(1'b0), ._4(Ovfl_soma), ._5(OVFL_sub), ._6(Ovfl__plus_1),
    ._7(Ovfl__1), .F(F), .S(S1_OVFL));
  ZERO zero_1 (.E(R), .S(S0_Zero));
  Negativo negativo_1 (.E(R), .NEG(S2_NEG));
endmodule
