// Digital circuit A-1.dig as structural Verilog
module A_1 (
  input  [15:0] A,
  output [15:0] S,
  output OVFL
);

  Subtracao_16bits subtracao_16bits_1 (.A(A), .B(16'h1), .S(S), .OVFL(OVFL));
endmodule
