// Digital circuit A_xor_B.dig as structural Verilog
module A_xor_B (
  input  [15:0] A,
  input  [15:0] B,
  output [15:0] S
);

  wire [15:0] and16bits_1_s, not_1_out, or16bits_1_s;

  AND16bits and16bits_1 (.A(A), .B(B), .S(and16bits_1_s));
  OR16bits or16bits_1 (.A(A), .B(B), .S(or16bits_1_s));
  assign not_1_out = ~and16bits_1_s;  // Not not_1, 16 bits wide
  AND16bits and16bits_2 (.A(not_1_out), .B(or16bits_1_s), .S(S));
endmodule
