// Digital circuit Deslocador_16bits.dig as structural Verilog
module Deslocador_16bits (
  input  [15:0] E,
  output [15:0] S
);

  mux2x1_1bit bit_0 (._0(1'b0), ._1(E[1]), .F(1'b0), .S(S[0]));
  mux2x1_1bit bit_1 (._0(E[0]), ._1(E[2]), .F(1'b0), .S(S[1]));
  mux2x1_1bit bit_2 (._0(E[1]), ._1(E[3]), .F(1'b0), .S(S[2]));
  mux2x1_1bit bit_3 (._0(E[2]), ._1(E[4]), .F(1'b0), .S(S[3]));
  mux2x1_1bit bit_4 (._0(E[3]), ._1(E[5]), .F(1'b0), .S(S[4]));
  mux2x1_1bit bit_5 (._0(E[4]), ._1(E[6]), .F(1'b0), .S(S[5]));
  mux2x1_1bit bit_6 (._0(E[5]), ._1(E[7]), .F(1'b0), .S(S[6]));
  mux2x1_1bit bit_7 (._0(E[6]), ._1(E[8]), .F(1'b0), .S(S[7]));
  mux2x1_1bit bit_8 (._0(E[7]), ._1(E[9]), .F(1'b0), .S(S[8]));
  mux2x1_1bit bit_9 (._0(E[8]), ._1(E[10]), .F(1'b0), .S(S[9]));
  mux2x1_1bit bit_10 (._0(E[9]), ._1(E[11]), .F(1'b0), .S(S[10]));
  mux2x1_1bit bit_11 (._0(E[10]), ._1(E[12]), .F(1'b0), .S(S[11]));
  mux2x1_1bit bit_12 (._0(E[11]), ._1(E[13]), .F(1'b0), .S(S[12]));
  mux2x1_1bit bit_13 (._0(E[12]), ._1(E[14]), .F(1'b0), .S(S[13]));
  mux2x1_1bit bit_14 (._0(E[13]), ._1(E[15]), .F(1'b0), .S(S[14]));
  mux2x1_1bit bit_15 (._0(E[14]), ._1(E[15]), .F(1'b0), .S(S[15]));

  // Other names for the same wires on the sheet: bit0_Entrada = E[0]; bit1_Entrada = E[1]; bit2_Entrada = E[2];
  //   bit3_Entrada = E[3]; bit4_Entrada = E[4]; bit5_Entrada = E[5]; bit6_Entrada = E[6]; bit7_Entrada = E[7];
  //   bit8_Entrada = E[8]; bit9_Entrada = E[9]; bit10_Entrada = E[10]; bit11_Entrada = E[11]; bit12_Entrada = E[12];
  //   bit13_Entrada = E[13]; bit14_Entrada = E[14]; bit15_Entrada = E[15]
endmodule
