// Digital circuit Deslocador_direita.dig as structural Verilog
module Deslocador_direita (
  input  [15:0] A,
  input  [15:0] B,
  output [15:0] S
);

  wire [15:0] bit1, bit2, bit3, bit4, bit5, bit6, bit7, bit8, bit9, bit10, bit11, bit12, bit13, bit14,
       deslocador_d_14_s;

  Deslocador_D deslocador_d_1 (.E(A), .S(bit1));
  Deslocador_D deslocador_d_2 (.E(bit8), .S(bit9));
  Deslocador_D deslocador_d_3 (.E(bit1), .S(bit2));
  Deslocador_D deslocador_d_4 (.E(bit9), .S(bit10));
  Deslocador_D deslocador_d_5 (.E(bit2), .S(bit3));
  Deslocador_D deslocador_d_6 (.E(bit10), .S(bit11));
  Deslocador_D deslocador_d_7 (.E(bit3), .S(bit4));
  Deslocador_D deslocador_d_8 (.E(bit11), .S(bit12));
  mux16x1 mux16x1_1 (
    ._0(A), ._1(bit1), ._2(bit2), ._3(bit3), ._4(bit4), ._5(bit5), ._6(bit6), ._7(bit7), ._8(bit8),
    ._9(bit9), ._10(bit10), ._11(bit11), ._12(bit12), ._13(bit13), ._14(bit14), ._15(deslocador_d_14_s),
    .F(B[3:0]), .S(S));
  Deslocador_D deslocador_d_9 (.E(bit4), .S(bit5));
  Deslocador_D deslocador_d_10 (.E(bit12), .S(bit13));
  Deslocador_D deslocador_d_11 (.E(bit5), .S(bit6));
  Deslocador_D deslocador_d_12 (.E(bit13), .S(bit14));
  Deslocador_D deslocador_d_13 (.E(bit6), .S(bit7));
  Deslocador_D deslocador_d_14 (.E(bit14), .S(deslocador_d_14_s));
  Deslocador_D deslocador_d_15 (.E(bit7), .S(bit8));

  // Other names for the same wires on the sheet: bit0[15:0] = A; C[15:0] = bit8
endmodule
