// Digital circuit Deslocador_esquerda.dig as structural Verilog
module Deslocador_esquerda (
  input  [15:0] A,
  input  [15:0] B,
  output [15:0] S
);

  wire [15:0] bit1, bit2, bit3, bit4, bit5, bit6, bit7, bit8, bit9, bit10, bit11, bit12, bit13, bit14,
       deslocador_16bits_14_s;

  Deslocador_16bits deslocador_16bits_1 (.E(A), .S(bit1));
  Deslocador_16bits deslocador_16bits_2 (.E(bit8), .S(bit9));
  Deslocador_16bits deslocador_16bits_3 (.E(bit1), .S(bit2));
  Deslocador_16bits deslocador_16bits_4 (.E(bit9), .S(bit10));
  Deslocador_16bits deslocador_16bits_5 (.E(bit2), .S(bit3));
  Deslocador_16bits deslocador_16bits_6 (.E(bit10), .S(bit11));
  Deslocador_16bits deslocador_16bits_7 (.E(bit3), .S(bit4));
  Deslocador_16bits deslocador_16bits_8 (.E(bit11), .S(bit12));
  mux16x1 mux16x1_1 (
    ._0(A), ._1(bit1), ._2(bit2), ._3(bit3), ._4(bit4), ._5(bit5), ._6(bit6), ._7(bit7), ._8(bit8),
    ._9(bit9), ._10(bit10), ._11(bit11), ._12(bit12), ._13(bit13), ._14(bit14), ._15(deslocador_16bits_14_s),
    .F(B[3:0]), .S(S));
  Deslocador_16bits deslocador_16bits_9 (.E(bit4), .S(bit5));
  Deslocador_16bits deslocador_16bits_10 (.E(bit12), .S(bit13));
  Deslocador_16bits deslocador_16bits_11 (.E(bit5), .S(bit6));
  Deslocador_16bits deslocador_16bits_12 (.E(bit13), .S(bit14));
  Deslocador_16bits deslocador_16bits_13 (.E(bit6), .S(bit7));
  Deslocador_16bits deslocador_16bits_14 (.E(bit14), .S(deslocador_16bits_14_s));
  Deslocador_16bits deslocador_16bits_15 (.E(bit7), .S(bit8));

  // Other names for the same wires on the sheet: bit0[15:0] = A; C[15:0] = bit8
endmodule
