// Digital circuit OR16bits.dig as structural Verilog
module OR16bits (
  input  [15:0] A,
  input  [15:0] B,
  output [15:0] S
);

  or or_1 (S[0], A[0], B[0]);
  or or_2 (S[1], A[1], B[1]);
  or or_3 (S[2], A[2], B[2]);
  or or_4 (S[3], A[3], B[3]);
  or or_5 (S[4], A[4], B[4]);
  or or_6 (S[5], A[5], B[5]);
  or or_7 (S[6], A[6], B[6]);
  or or_8 (S[7], A[7], B[7]);
  or or_9 (S[8], A[8], B[8]);
  or or_10 (S[9], A[9], B[9]);
  or or_11 (S[10], A[10], B[10]);
  or or_12 (S[11], A[11], B[11]);
  or or_13 (S[12], A[12], B[12]);
  or or_14 (S[13], A[13], B[13]);
  or or_15 (S[14], A[14], B[14]);
  or or_16 (S[15], A[15], B[15]);

  // Other names for the same wires on the sheet: Abit0 = A[0]; Abit1 = A[1]; Abit2 = A[2]; Abit3 = A[3]; Abit4 = A[4];
  //   Abit5 = A[5]; Abit6 = A[6]; Abit7 = A[7]; Abit8 = A[8]; Abit9 = A[9]; Abit10 = A[10]; Abit11 = A[11];
  //   Abit12 = A[12]; Abit13 = A[13]; Abit14 = A[14]; Abit15 = A[15]; Bbit0 = B[0]; Bbit1 = B[1]; Bbit2 = B[2];
  //   Bbit3 = B[3]; Bbit4 = B[4]; Bbit5 = B[5]; Bbit6 = B[6]; Bbit7 = B[7]; Bbit8 = B[8]; Bbit9 = B[9];
  //   Bbit10 = B[10]; Bbit11 = B[11]; Bbit12 = B[12]; Bbit13 = B[13]; Bbit14 = B[14]; Bbit15 = B[15]; Sbit0 = S[0];
  //   Sbit1 = S[1]; Sbit2 = S[2]; Sbit3 = S[3]; Sbit4 = S[4]; Sbit5 = S[5]; Sbit6 = S[6]; Sbit7 = S[7]; Sbit8 = S[8];
  //   Sbit9 = S[9]; Sbit10 = S[10]; Sbit11 = S[11]; Sbit12 = S[12]; Sbit13 = S[13]; Sbit14 = S[14]; Sbit15 = S[15]
endmodule
