// Digital circuit Subtracao_16bits.dig as structural Verilog
module Subtracao_16bits (
  input  [15:0] A,
  input  [15:0] B,
  output [15:0] S,
  output OVFL
);

  wire [15:0] not_1_out, somador_completo16bits_1_s;

  assign not_1_out = ~B;  // Not not_1, 16 bits wide
  somador_completo16bits somador_completo16bits_1 (
    .A(not_1_out), .B(16'h1), .S(somador_completo16bits_1_s));  // open: OVFL
  somador_completo16bits somador_completo16bits_2 (.A(A), .B(somador_completo16bits_1_s), .S(S), .OVFL(OVFL));
endmodule
