// Digital circuit ZERO.dig as structural Verilog
module ZERO (
  input  [15:0] E,
  output S
);

  wire or_1_out;

  or or_1 (or_1_out, E[15], E[14], E[13], E[12], E[11], E[10], E[9], E[8], E[7], E[6], E[5], E[4], E[3], E[2], E[1], E[0]);
  not not_1 (S, or_1_out);

  // Other names for the same wires on the sheet: _1 = E[0]; _2 = E[1]; _3 = E[2]; _4 = E[3]; _5 = E[4]; _6 = E[5];
  //   _7 = E[6]; _8 = E[7]; _9 = E[8]; _10 = E[9]; _11 = E[10]; _12 = E[11]; _13 = E[12]; _14 = E[13]; _15 = E[14];
  //   _16 = E[15]
endmodule
