// Digital circuit mux16x1.dig as structural Verilog
module mux16x1 (
  input  [15:0] _0,
  input  [15:0] _1,
  input  [15:0] _2,
  input  [15:0] _3,
  input  [15:0] _4,
  input  [15:0] _5,
  input  [15:0] _6,
  input  [15:0] _7,
  input  [15:0] _8,
  input  [15:0] _9,
  input  [15:0] _10,
  input  [15:0] _11,
  input  [15:0] _12,
  input  [15:0] _13,
  input  [15:0] _14,
  input  [15:0] _15,
  input  [3:0] F,
  output [15:0] S
);

  wire [15:0] mux8x1_1_s, mux8x1_2_s;

  mux8x1 mux8x1_1 (._0(_0), ._1(_1), ._2(_2), ._3(_3), ._4(_4), ._5(_5), ._6(_6), ._7(_7), .F(F[2:0]), .S(mux8x1_1_s));
  mux8x1 mux8x1_2 (
    ._0(_8), ._1(_9), ._2(_10), ._3(_11), ._4(_12), ._5(_13), ._6(_14), ._7(_15), .F(F[2:0]), .S(mux8x1_2_s));
  mux2x1 mux2x1_1 (._0(mux8x1_1_s), ._1(mux8x1_2_s), .S(S), .F(F[3]));

  // Other names for the same wires on the sheet: F0_2[2:0] = F[2:0]
endmodule
