// Digital circuit mux2x1.dig as structural Verilog
module mux2x1 (
  input  [15:0] _0,
  input  [15:0] _1,
  input  F,
  output [15:0] S
);

  wire [15:0] and16bits_1_s, and16bits_2_s, not_1_out;

  AND16bits and16bits_1 (.A(_0), .B(not_1_out), .S(and16bits_1_s));
  assign not_1_out = ~{16{F}};  // Not not_1, 16 bits wide
  AND16bits and16bits_2 (.A(_1), .B({16{F}}), .S(and16bits_2_s));
  OR16bits or16bits_1 (.A(and16bits_1_s), .B(and16bits_2_s), .S(S));
endmodule
