// Digital circuit mux4x1.dig as structural Verilog
module mux4x1 (
  input  [15:0] _0,
  input  [15:0] _1,
  input  [15:0] _2,
  input  [15:0] _3,
  input  [1:0] F,
  output [15:0] S
);

  wire [15:0] mux2x1_1_s, mux2x1_2_s;

  mux2x1 mux2x1_1 (._0(_0), ._1(_1), .S(mux2x1_1_s), .F(F[0]));
  mux2x1 mux2x1_2 (._0(_2), ._1(_3), .S(mux2x1_2_s), .F(F[0]));
  mux2x1 mux2x1_3 (._0(mux2x1_1_s), ._1(mux2x1_2_s), .S(S), .F(F[1]));
endmodule
