// Digital circuit mux4x1_1bit.dig as structural Verilog
module mux4x1_1bit (
  input  _0,
  input  _1,
  input  _2,
  input  _3,
  input  [1:0] F,
  output S
);

  wire mux2x1_1bit_1_s, mux2x1_1bit_2_s;

  mux2x1_1bit mux2x1_1bit_1 (._0(_0), ._1(_1), .F(F[0]), .S(mux2x1_1bit_1_s));
  mux2x1_1bit mux2x1_1bit_2 (._0(_2), ._1(_3), .F(F[0]), .S(mux2x1_1bit_2_s));
  mux2x1_1bit mux2x1_1bit_3 (._0(mux2x1_1bit_1_s), ._1(mux2x1_1bit_2_s), .F(F[1]), .S(S));
endmodule
