// Digital circuit mux8x1.dig as structural Verilog
module mux8x1 (
  input  [15:0] _0,
  input  [15:0] _1,
  input  [15:0] _2,
  input  [15:0] _3,
  input  [15:0] _4,
  input  [15:0] _5,
  input  [15:0] _6,
  input  [15:0] _7,
  input  [2:0] F,
  output [15:0] S
);

  wire [15:0] mux4x1_1_s, mux4x1_2_s;

  mux4x1 mux4x1_1 (._0(_0), ._1(_1), ._2(_2), ._3(_3), .F(F[1:0]), .S(mux4x1_1_s));
  mux4x1 mux4x1_2 (._0(_4), ._1(_5), ._2(_6), ._3(_7), .F(F[1:0]), .S(mux4x1_2_s));
  mux2x1 mux2x1_1 (._0(mux4x1_1_s), ._1(mux4x1_2_s), .S(S), .F(F[2]));

  // Other names for the same wires on the sheet: F0[1:0] = F[1:0]; F1 = F[2]
endmodule
