// Digital circuit mux8x1_1bit.dig as structural Verilog
module mux8x1_1bit (
  input  _0,
  input  _1,
  input  _2,
  input  _3,
  input  _4,
  input  _5,
  input  _6,
  input  _7,
  input  [2:0] F,
  output S
);

  wire mux4x1_1bit_1_s, mux4x1_1bit_2_s;

  mux4x1_1bit mux4x1_1bit_1 (._0(_0), ._1(_1), ._2(_2), ._3(_3), .F(F[1:0]), .S(mux4x1_1bit_1_s));
  mux4x1_1bit mux4x1_1bit_2 (._0(_4), ._1(_5), ._2(_6), ._3(_7), .F(F[1:0]), .S(mux4x1_1bit_2_s));
  mux2x1_1bit mux2x1_1bit_1 (._0(mux4x1_1bit_1_s), ._1(mux4x1_1bit_2_s), .F(F[2]), .S(S));

  // Other names for the same wires on the sheet: F0[1:0] = F[1:0]; F1 = F[2]
endmodule
