// Digital circuit shor1bit.dig as structural Verilog
module shor1bit (
  input  A,
  input  B,
  output S
);

  wire nand_1_out, or_1_out;

  nand nand_1 (nand_1_out, A, B);
  or or_1 (or_1_out, B, A);
  and and_1 (S, nand_1_out, or_1_out);
endmodule
