// Digital circuit somador_completo.dig as structural Verilog
module somador_completo (
  input  A,
  input  B,
  input  Ci,
  output Co,
  output S
);

  wire and_1_out, and_2_out, and_3_out, xor_1_out;

  xor xor_1 (xor_1_out, A, B);
  and and_1 (and_1_out, Ci, A);
  and and_2 (and_2_out, Ci, B);
  and and_3 (and_3_out, B, A);
  xor xor_2 (S, xor_1_out, Ci);
  or or_1 (Co, and_1_out, and_2_out, and_3_out);
endmodule
