// Digital circuit somador_completo16bits.dig as structural Verilog
module somador_completo16bits (
  input  [15:0] A,
  input  [15:0] B,
  output [15:0] S,
  output OVFL
);

  wire somador_completo_1_co, somador_completo_2_co, somador_completo_3_co, somador_completo_4_co,
       somador_completo_5_co, somador_completo_6_co, somador_completo_7_co, somador_completo_8_co,
       somador_completo_9_co, somador_completo_10_co, somador_completo_11_co, somador_completo_12_co,
       somador_completo_13_co, somador_completo_14_co, somador_completo_15_co, somador_completo_16_co;

  somador_completo somador_completo_1 (.A(A[0]), .B(B[0]), .Ci(1'b0), .Co(somador_completo_1_co), .S(S[0]));
  somador_completo somador_completo_2 (
    .A(A[1]), .B(B[1]), .Ci(somador_completo_1_co), .Co(somador_completo_2_co), .S(S[1]));
  somador_completo somador_completo_3 (
    .A(A[2]), .B(B[2]), .Ci(somador_completo_2_co), .Co(somador_completo_3_co), .S(S[2]));
  somador_completo somador_completo_4 (
    .A(A[3]), .B(B[3]), .Ci(somador_completo_3_co), .Co(somador_completo_4_co), .S(S[3]));
  somador_completo somador_completo_5 (
    .A(A[4]), .B(B[4]), .Ci(somador_completo_4_co), .Co(somador_completo_5_co), .S(S[4]));
  somador_completo somador_completo_6 (
    .A(A[5]), .B(B[5]), .Ci(somador_completo_5_co), .Co(somador_completo_6_co), .S(S[5]));
  somador_completo somador_completo_7 (
    .A(A[6]), .B(B[6]), .Ci(somador_completo_6_co), .Co(somador_completo_7_co), .S(S[6]));
  somador_completo somador_completo_8 (
    .A(A[7]), .B(B[7]), .Ci(somador_completo_7_co), .Co(somador_completo_8_co), .S(S[7]));
  somador_completo somador_completo_9 (
    .A(A[8]), .B(B[8]), .Ci(somador_completo_8_co), .Co(somador_completo_9_co), .S(S[8]));
  somador_completo somador_completo_10 (
    .A(A[9]), .B(B[9]), .Ci(somador_completo_9_co), .Co(somador_completo_10_co), .S(S[9]));
  somador_completo somador_completo_11 (
    .A(A[10]), .B(B[10]), .Ci(somador_completo_10_co), .Co(somador_completo_11_co), .S(S[10]));
  somador_completo somador_completo_12 (
    .A(A[11]), .B(B[11]), .Ci(somador_completo_11_co), .Co(somador_completo_12_co), .S(S[11]));
  somador_completo somador_completo_13 (
    .A(A[12]), .B(B[12]), .Ci(somador_completo_12_co), .Co(somador_completo_13_co), .S(S[12]));
  somador_completo somador_completo_14 (
    .A(A[13]), .B(B[13]), .Ci(somador_completo_13_co), .Co(somador_completo_14_co), .S(S[13]));
  somador_completo somador_completo_15 (
    .A(A[14]), .B(B[14]), .Ci(somador_completo_14_co), .Co(somador_completo_15_co), .S(S[14]));
  somador_completo somador_completo_16 (
    .A(A[15]), .B(B[15]), .Ci(somador_completo_15_co), .Co(somador_completo_16_co), .S(S[15]));
  xor xor_1 (OVFL, somador_completo_15_co, somador_completo_16_co);

  // Other names for the same wires on the sheet: Abit0 = A[0]; Abit1 = A[1]; Abit2 = A[2]; Abit3 = A[3]; Abit4 = A[4];
  //   Abit5 = A[5]; Abit6 = A[6]; Abit7 = A[7]; Abit8 = A[8]; Abit9 = A[9]; Abit10 = A[10]; Abit11 = A[11];
  //   Abit12 = A[12]; Abit13 = A[13]; Abit14 = A[14]; Abit15 = A[15]; Bbit0 = B[0]; Bbit1 = B[1]; Bbit2 = B[2];
  //   Bbit3 = B[3]; Bbit4 = B[4]; Bbit5 = B[5]; Bbit6 = B[6]; Bbit7 = B[7]; Bbit8 = B[8]; Bbit9 = B[9];
  //   Bbit10 = B[10]; Bbit11 = B[11]; Bbit12 = B[12]; Bbit13 = B[13]; Bbit14 = B[14]; Bbit15 = B[15]
endmodule
