// Logisim project MicroProcessador.circ as structural Verilog: 6 circuits, main circuit main
module main (
  input  reset,
  input  in_2,
  output [7:0] out_3
);

  wire ALUfonte, branch_out, clock_1_out, finaliza, jal_pc, jalr_pc, Jump, Memread, MemToReg, Memwrite,
       multiplexer_1_out, not_1_out, reg_ent, regwrite;
  wire [1:0] branch;
  wire [3:0] ALUop;
  wire [4:0] Jump_imm, multiplexer_5_out, multiplexer_6_out, Rd;
  wire [5:0] Memoria_ROM_data;
  wire [7:0] adder_2_out, adder_3_out, Imm, multiplexer_2_out, multiplexer_3_out, PC_q, Pcadd1;
  wire [23:0] Banco_Registradores_registrador_lido_1, bit_extender_1_out, bit_extender_2_out, cont_rs2,
       jumpR, Memoria_Ram_dout, multiplexer_7_out, multiplexer_8_out, multiplexer_9_out;

  Clock clock_1 (.out(clock_1_out));
  Multiplexer multiplexer_1 (.in0(finaliza), .in1(reset), .out(multiplexer_1_out), .sel(in_2));
  Register PC (.D(out_3), .Q(PC_q), .clk(clock_1_out), .clr(multiplexer_1_out));  // open: en
  Adder adder_1 (.a(8'h1), .b(PC_q), .out(Pcadd1));  // open: cin, cout
  ROM #(.dataWidth(24)) Memoria_ROM (.addr(PC_q), .data({Imm, Jump_imm, Rd, Memoria_ROM_data}));
  Adder adder_2 (.a({Imm[2:0], Jump_imm}), .b(PC_q), .out(adder_2_out));  // open: cin, cout
  Multiplexer #(.width(8)) multiplexer_2 (.in0(Pcadd1), .in1(adder_2_out), .out(multiplexer_2_out), .sel(jal_pc));
  Adder adder_3 (.a(Imm), .b(PC_q), .out(adder_3_out));  // open: cin, cout
  Multiplexer #(.width(8)) multiplexer_3 (
    .in0(multiplexer_2_out), .in1(adder_3_out), .out(multiplexer_3_out), .sel(branch_out));
  Multiplexer #(.width(8)) multiplexer_4 (.in0(multiplexer_3_out), .in1(jumpR[7:0]), .out(out_3), .sel(jalr_pc));
  Multiplexer #(.width(5)) multiplexer_5 (.in0(Jump_imm), .in1(Rd), .out(multiplexer_5_out), .sel(reg_ent));
  Multiplexer #(.width(5)) multiplexer_6 (.in0(Imm[4:0]), .in1(Jump_imm), .out(multiplexer_6_out), .sel(reg_ent));
  Unidade_de_controle UC (
    .in_1(Memoria_ROM_data), .RegWrite(regwrite), .ALUFont(ALUfonte), .MemRead(Memread), .MemWrite(Memwrite),
    .MemtoReg(MemToReg), .Branch(branch), .Jump(Jump), .ALUop(ALUop), .reg_ent(reg_ent), .jal_pc(jal_pc),
    .jalr_pc(jalr_pc), .finaliza(finaliza));
  Banco_de_Registradores Banco_Registradores (
    .Ler_Registrador1(multiplexer_5_out), .Ler_Registrador2(multiplexer_6_out),
    .Escreve_Dados(multiplexer_8_out), .Registrador_Escrito(Rd), .Escrever_no_Registrador(regwrite),
    .CLK(clock_1_out), .CLEAR(multiplexer_1_out),
    .Registrador_lido_1(Banco_Registradores_registrador_lido_1), .Registrador_lido_2(cont_rs2));
  Multiplexer #(.width(24)) multiplexer_7 (
    .in0(cont_rs2), .in1(bit_extender_1_out), .out(multiplexer_7_out), .sel(ALUfonte));
  assign bit_extender_1_out = {{16{Imm[7]}}, Imm};  // Bit_Extender bit_extender_1
  Multiplexer #(.width(24)) multiplexer_8 (
    .in0(multiplexer_9_out), .in1(bit_extender_2_out), .out(multiplexer_8_out), .sel(Jump));
  branchs Banco_de_Branchs (
    .rs1(Banco_Registradores_registrador_lido_1), .rs2(cont_rs2), .in_3(branch), .out_4(branch_out));
  Bit_Extender #(.out_width(24), .\type ("input")) bit_extender_2 (
    .in(Pcadd1), .out(bit_extender_2_out));  // open: extend
  Multiplexer #(.width(24)) multiplexer_9 (
    .in0(jumpR), .in1(Memoria_Ram_dout), .out(multiplexer_9_out), .sel(MemToReg));
  ULA Ula_Micro (
    .En_A(Banco_Registradores_registrador_lido_1), .En_B(multiplexer_7_out), .instrucao(ALUop), .out_4(jumpR));  // open: Zero
  not not_1 (not_1_out, clock_1_out);
  RAM #(.dataWidth(24)) Memoria_Ram (
    .addr(jumpR[7:0]), .we(Memwrite), .oe(Memread), .clk(not_1_out), .din(cont_rs2), .dout(Memoria_Ram_dout));

  // Other names for the same wires on the sheet: Rs1_B_S[4:0] = Rd; Jump_imm[12:5] = Imm; Rs2[4:0] = Imm[4:0];
  //   Rs1[4:0] = Jump_imm; Rs2_B_S[4:0] = Jump_imm

  // Notes on the sheet:
  //   contents of Memoria_ROM (hex, n*v repeats v):
  //   30084 0 500c4 0 21901 0 20184 0 3310d 0 0 0 1850 0 180c 4*0 1cb 0 0 0 13
endmodule

// Registrador 1 - x0
module Banco_de_Registradores (
  input  [4:0] Ler_Registrador1,
  input  [4:0] Ler_Registrador2,
  input  [23:0] Escreve_Dados,
  input  [4:0] Registrador_Escrito,
  input  Escrever_no_Registrador,
  input  CLK,
  input  CLEAR,
  output [23:0] Registrador_lido_1,
  output [23:0] Registrador_lido_2
);

  wire Enable_x1, Enable_x2, Enable_x3, Enable_x4, Enable_x5, Enable_x6, Enable_x7, Enable_x8, Enable_x9,
       Enable_x10, Enable_x11, Enable_x12, Enable_x13, Enable_x14, Enable_x15, Enable_x16, Enable_x17,
       Enable_x18, Enable_x19, Enable_x20, Enable_x21, Enable_x22, Enable_x23, Enable_x24, Enable_x25,
       Enable_x26, Enable_x27, Enable_x28, Enable_x29, Enable_x30, Enable_x31;
  wire [23:0] WRx1, WRx2, WRx3, WRx4, WRx5, WRx6, WRx7, WRx8, WRx9, WRx10, WRx11, WRx12, WRx13, WRx14, WRx15,
       WRx16, WRx17, WRx18, WRx19, WRx20, WRx21, WRx22, WRx23, WRx24, WRx25, WRx26, WRx27, WRx28, WRx29,
       WRx30, WRx31, x0, x1, x2, x3, x4, x5, x6, x7, x8, x9, x10, x11, x12, x13, x14, x15, x16, x17, x18,
       x19, x20, x21, x22, x23, x24, x25, x26, x27, x28, x29, x30, x31;

  Demultiplexer #(.select(5), .width(24)) demultiplexer_1 (
    .out1(WRx1), .out2(WRx2), .out3(WRx3), .out4(WRx4), .out5(WRx5), .out6(WRx6), .out7(WRx7), .out8(WRx8),
    .out9(WRx9), .out10(WRx10), .out11(WRx11), .out12(WRx12), .out13(WRx13), .out14(WRx14), .out15(WRx15),
    .out16(WRx16), .out17(WRx17), .out18(WRx18), .out19(WRx19), .out20(WRx20), .out21(WRx21), .out22(WRx22),
    .out23(WRx23), .out24(WRx24), .out25(WRx25), .out26(WRx26), .out27(WRx27), .out28(WRx28), .out29(WRx29),
    .out30(WRx30), .out31(WRx31), .in(Escreve_Dados), .sel(Registrador_Escrito));  // open: out0
  Demultiplexer #(.select(5)) demultiplexer_2 (
    .out1(Enable_x1), .out2(Enable_x2), .out3(Enable_x3), .out4(Enable_x4), .out5(Enable_x5),
    .out6(Enable_x6), .out7(Enable_x7), .out8(Enable_x8), .out9(Enable_x9), .out10(Enable_x10),
    .out11(Enable_x11), .out12(Enable_x12), .out13(Enable_x13), .out14(Enable_x14), .out15(Enable_x15),
    .out16(Enable_x16), .out17(Enable_x17), .out18(Enable_x18), .out19(Enable_x19), .out20(Enable_x20),
    .out21(Enable_x21), .out22(Enable_x22), .out23(Enable_x23), .out24(Enable_x24), .out25(Enable_x25),
    .out26(Enable_x26), .out27(Enable_x27), .out28(Enable_x28), .out29(Enable_x29), .out30(Enable_x30),
    .out31(Enable_x31), .in(Escrever_no_Registrador), .sel(Registrador_Escrito));  // open: out0
  Register #(.width(24)) u_x0 (.D({24{1'b0}}), .en(1'b1), .Q(x0), .clk(CLK), .clr(CLEAR));
  Register #(.width(24)) u_x8 (.D(WRx8), .en(Enable_x8), .Q(x8), .clk(CLK), .clr(CLK));
  Register #(.width(24)) u_x16 (.D(WRx16), .en(Enable_x16), .Q(x16), .clk(CLK), .clr(CLEAR));
  Register #(.width(24)) u_x24 (.D(WRx24), .en(Enable_x24), .Q(x24), .clk(CLK), .clr(CLEAR));
  Register #(.width(24)) u_x1 (.D(WRx1), .en(Enable_x1), .Q(x1), .clk(CLK), .clr(CLEAR));
  Register #(.width(24)) u_x9 (.D(WRx9), .en(Enable_x9), .Q(x9), .clk(CLK), .clr(CLK));
  Register #(.width(24)) u_x17 (.D(WRx17), .en(Enable_x17), .Q(x17), .clk(CLK), .clr(CLEAR));
  Register #(.width(24)) u_x25 (.D(WRx25), .en(Enable_x25), .Q(x25), .clk(CLK), .clr(CLEAR));
  Register #(.width(24)) u_x2 (.D(WRx2), .en(Enable_x2), .Q(x2), .clk(CLK), .clr(CLEAR));
  Register #(.width(24)) u_x10 (.D(WRx10), .en(Enable_x10), .Q(x10), .clk(CLK), .clr(CLK));
  Register #(.width(24)) u_x18 (.D(WRx18), .en(Enable_x18), .Q(x18), .clk(CLK), .clr(CLEAR));
  Register #(.width(24)) u_x26 (.D(WRx26), .en(Enable_x26), .Q(x26), .clk(CLK), .clr(CLEAR));
  Register #(.width(24)) u_x3 (.D(WRx3), .en(Enable_x3), .Q(x3), .clk(CLK), .clr(CLEAR));
  Register #(.width(24)) u_x11 (.D(WRx11), .en(Enable_x11), .Q(x11), .clk(CLK), .clr(CLK));
  Register #(.width(24)) u_x19 (.D(WRx19), .en(Enable_x19), .Q(x19), .clk(CLK), .clr(CLEAR));
  Register #(.width(24)) u_x27 (.D(WRx27), .en(Enable_x27), .Q(x27), .clk(CLK), .clr(CLEAR));
  Register #(.width(24)) u_x4 (.D(WRx4), .en(Enable_x4), .Q(x4), .clk(CLK), .clr(CLEAR));
  Register #(.width(24)) u_x12 (.D(WRx12), .en(Enable_x12), .Q(x12), .clk(CLK), .clr(CLK));
  Register #(.width(24)) u_x20 (.D(WRx20), .en(Enable_x20), .Q(x20), .clk(CLK), .clr(CLEAR));
  Register #(.width(24)) u_x28 (.D(WRx28), .en(Enable_x28), .Q(x28), .clk(CLK), .clr(CLEAR));
  Register #(.width(24)) u_x5 (.D(WRx5), .en(Enable_x5), .Q(x5), .clk(CLK), .clr(CLEAR));
  Register #(.width(24)) u_x13 (.D(WRx13), .en(Enable_x13), .Q(x13), .clk(CLK), .clr(CLK));
  Register #(.width(24)) u_x21 (.D(WRx21), .en(Enable_x21), .Q(x21), .clk(CLK), .clr(CLEAR));
  Register #(.width(24)) u_x29 (.D(WRx29), .en(Enable_x29), .Q(x29), .clk(CLK), .clr(CLEAR));
  Register #(.width(24)) u_x6 (.D(WRx6), .en(Enable_x6), .Q(x6), .clk(CLK), .clr(CLEAR));
  Register #(.width(24)) u_x14 (.D(WRx14), .en(Enable_x14), .Q(x14), .clk(CLK), .clr(CLK));
  Register #(.width(24)) u_x22 (.D(WRx22), .en(Enable_x22), .Q(x22), .clk(CLK), .clr(CLEAR));
  Register #(.width(24)) u_x30 (.D(WRx30), .en(Enable_x30), .Q(x30), .clk(CLK), .clr(CLEAR));
  Register #(.width(24)) u_x7 (.D(WRx7), .en(Enable_x7), .Q(x7), .clk(CLK), .clr(CLEAR));
  Register #(.width(24)) u_x15 (.D(WRx15), .en(Enable_x15), .Q(x15), .clk(CLK), .clr(CLK));
  Register #(.width(24)) u_x23 (.D(WRx23), .en(Enable_x23), .Q(x23), .clk(CLK), .clr(CLEAR));
  Register #(.width(24)) u_x31 (.D(WRx31), .en(Enable_x31), .Q(x31), .clk(CLK), .clr(CLEAR));
  Multiplexer #(.select(5), .width(24)) multiplexer_1 (
    .in0(x0), .in1(x1), .in2(x2), .in3(x3), .in4(x4), .in5(x5), .in6(x6), .in7(x7), .in8(x8), .in9(x9),
    .in10(x10), .in11(x11), .in12(x12), .in13(x13), .in14(x14), .in15(x15), .in16(x16), .in17(x17),
    .in18(x18), .in19(x19), .in20(x20), .in21(x21), .in22(x22), .in23(x23), .in24(x24), .in25(x25),
    .in26(x26), .in27(x27), .in28(x28), .in29(x29), .in30(x30), .in31(x31), .out(Registrador_lido_1),
    .sel(Ler_Registrador1));
  Multiplexer #(.select(5), .width(24)) multiplexer_2 (
    .in0(x0), .in1(x1), .in2(x2), .in3(x3), .in4(x4), .in5(x5), .in6(x6), .in7(x7), .in8(x8), .in9(x9),
    .in10(x10), .in11(x11), .in12(x12), .in13(x13), .in14(x14), .in15(x15), .in16(x16), .in17(x17),
    .in18(x18), .in19(x19), .in20(x20), .in21(x21), .in22(x22), .in23(x23), .in24(x24), .in25(x25),
    .in26(x26), .in27(x27), .in28(x28), .in29(x29), .in30(x30), .in31(x31), .out(Registrador_lido_2),
    .sel(Ler_Registrador2));

  // Other names for the same wires on the sheet: RS1[4:0] = Ler_Registrador1; RS2[4:0] = Ler_Registrador2
endmodule

module ULA (
  input  [23:0] En_A,
  input  [23:0] En_B,
  input  [3:0] instrucao,
  output [23:0] out_4,
  output Zero
);

  wire [4:0] bit_extender_1_out, bit_extender_2_out, bit_extender_3_out;
  wire [23:0] A_And, A_Div, A_Mul, A_Or, A_Sll, A_Soma, A_Sra, A_Srl, A_Sub, A_Xor, adder_1_out, and_1_out,
       B_And, B_Div, B_Mul, B_Or, B_Sll, B_Soma, B_Sra, B_Srl, B_Sub, B_Xor, divider_1_out, multiplier_1_out,
       or_1_out, shifter_1_out, shifter_2_out, shifter_3_out, subtractor_1_out, xor_1_out;

  Demultiplexer #(.select(4), .width(24)) demultiplexer_1 (
    .out0(B_Soma), .out1(B_Sub), .out2(B_Mul), .out3(B_Div), .out4(B_And), .out5(B_Or), .out6(B_Xor),
    .out7(B_Sll), .out8(B_Srl), .out9(B_Sra), .in(En_B), .sel(instrucao));  // open: out10, out11, out12, out13, out14, out15
  Demultiplexer #(.select(4), .width(24)) demultiplexer_2 (
    .out0(A_Soma), .out1(A_Sub), .out2(A_Mul), .out3(A_Div), .out4(A_And), .out5(A_Or), .out6(A_Xor),
    .out7(A_Sll), .out8(A_Srl), .out9(A_Sra), .in(En_A), .sel(instrucao));  // open: out10, out11, out12, out13, out14, out15
  Bit_Extender #(.in_width(24), .out_width(5), .\type ("input")) bit_extender_1 (
    .in(B_Sll), .out(bit_extender_1_out));  // open: extend
  Bit_Extender #(.in_width(24), .out_width(5), .\type ("input")) bit_extender_2 (
    .in(B_Srl), .out(bit_extender_2_out));  // open: extend
  Bit_Extender #(.in_width(24), .out_width(5), .\type ("input")) bit_extender_3 (
    .in(B_Sra), .out(bit_extender_3_out));  // open: extend
  Adder #(.width(24)) adder_1 (.a(A_Soma), .b(B_Soma), .out(adder_1_out));  // open: cin, cout
  Subtractor #(.width(24)) subtractor_1 (.a(A_Sub), .b(B_Sub), .out(subtractor_1_out));  // open: bin, bout
  Multiplier #(.mode("twosComplement"), .width(24)) multiplier_1 (
    .a(A_Mul), .b(B_Mul), .out(multiplier_1_out));  // open: cin, cout
  Divider #(.width(24)) divider_1 (.a(A_Div), .b(B_Div), .out(divider_1_out));  // open: upper, rem
  assign and_1_out = A_And & B_And;  // AND_Gate and_1, 24 bits wide
  assign or_1_out = A_Or | B_Or;  // OR_Gate or_1, 24 bits wide
  assign xor_1_out = A_Xor ^ B_Xor;  // XOR_Gate xor_1, 24 bits wide
  Shifter #(.width(24)) shifter_1 (.in(A_Sll), .\dist (bit_extender_1_out), .out(shifter_1_out));
  Shifter #(.shift("lr"), .width(24)) shifter_2 (.in(A_Srl), .\dist (bit_extender_2_out), .out(shifter_2_out));
  Shifter #(.shift("ar"), .width(24)) shifter_3 (.in(A_Sra), .\dist (bit_extender_3_out), .out(shifter_3_out));
  Multiplexer #(.select(4), .width(24)) multiplexer_1 (
    .in0(adder_1_out), .in1(subtractor_1_out), .in2(multiplier_1_out), .in3(divider_1_out), .in4(and_1_out),
    .in5(or_1_out), .in6(xor_1_out), .in7(shifter_1_out), .in8(shifter_2_out), .in9(shifter_3_out),
    .out(out_4), .sel(instrucao));  // open: in10, in11, in12, in13, in14, in15
  Verifica_0 verifica_0_1 (.in_1(out_4), .out_2(Zero));

  // Other names for the same wires on the sheet: Inst[3:0] = instrucao

  // Notes on the sheet:
  //   000000
  //   000001
  //   000010
  //   000011
  //   000100
  //   000101
  //   000110
  //   000111
  //   001000
  //   001001
endmodule

module Verifica_0 (
  input  [23:0] in_1,
  output out_2
);

  nor nor_1 (out_2, in_1[0], in_1[1], in_1[2], in_1[3], in_1[4], in_1[5], in_1[6], in_1[7], in_1[8], in_1[9], in_1[10], in_1[11], in_1[12], in_1[13], in_1[14], in_1[15], in_1[16], in_1[17], in_1[18], in_1[19], in_1[20], in_1[21], in_1[22], in_1[23]);
endmodule

module Unidade_de_controle (
  input  [5:0] in_1,
  output RegWrite,
  output ALUFont,
  output MemRead,
  output MemWrite,
  output MemtoReg,
  output [1:0] Branch,
  output Jump,
  output [3:0] ALUop,
  output reg_ent,
  output jal_pc,
  output jalr_pc,
  output finaliza
);

  wire add_out, addi_out, and_1_out, and_2_out, and_3_out, and_4_out, and_out, beq_out, blt_out, bne_out,
       div_out, mul_out, nfn_out, or_out, sll_out, sra_out, srl_out, sub_out, xor_out;

  and Add (add_out, ~in_1[0], ~in_1[1], ~in_1[2], ~in_1[3], ~in_1[4], ~in_1[5]);  // AND_Gate
  and Sub (sub_out, in_1[0], ~in_1[1], ~in_1[2], ~in_1[3], ~in_1[4], ~in_1[5]);  // AND_Gate
  and Mul (mul_out, ~in_1[0], in_1[1], ~in_1[2], ~in_1[3], ~in_1[4], ~in_1[5]);  // AND_Gate
  and Div (div_out, in_1[0], in_1[1], ~in_1[2], ~in_1[3], ~in_1[4], ~in_1[5]);  // AND_Gate
  and AddI (addi_out, ~in_1[0], ~in_1[1], in_1[2], ~in_1[3], ~in_1[4], ~in_1[5]);  // AND_Gate
  and And_logico (and_out, in_1[0], ~in_1[1], in_1[2], ~in_1[3], ~in_1[4], ~in_1[5]);  // AND_Gate
  and Or_logico (or_out, ~in_1[0], in_1[1], in_1[2], ~in_1[3], ~in_1[4], ~in_1[5]);  // AND_Gate
  and Xor_logico (xor_out, in_1[0], in_1[1], in_1[2], ~in_1[3], ~in_1[4], ~in_1[5]);  // AND_Gate
  and Sll0 (sll_out, ~in_1[0], ~in_1[1], ~in_1[2], in_1[3], ~in_1[4], ~in_1[5]);  // AND_Gate
  and Srl0 (srl_out, in_1[0], ~in_1[1], ~in_1[2], in_1[3], ~in_1[4], ~in_1[5]);  // AND_Gate
  and Sra0 (sra_out, ~in_1[0], in_1[1], ~in_1[2], in_1[3], ~in_1[4], ~in_1[5]);  // AND_Gate
  and Lw (MemRead, in_1[0], in_1[1], ~in_1[2], in_1[3], ~in_1[4], ~in_1[5]);  // AND_Gate
  and Sw (MemWrite, ~in_1[0], ~in_1[1], in_1[2], in_1[3], ~in_1[4], ~in_1[5]);  // AND_Gate
  and Beq (beq_out, in_1[0], ~in_1[1], in_1[2], in_1[3], ~in_1[4], ~in_1[5]);  // AND_Gate
  and Bne (bne_out, ~in_1[0], in_1[1], in_1[2], in_1[3], ~in_1[4], ~in_1[5]);  // AND_Gate
  and Blt (blt_out, in_1[0], in_1[1], in_1[2], in_1[3], ~in_1[4], ~in_1[5]);  // AND_Gate
  and Jal (jal_pc, ~in_1[0], ~in_1[1], ~in_1[2], ~in_1[3], in_1[4], ~in_1[5]);  // AND_Gate
  and Jalr (jalr_pc, in_1[0], ~in_1[1], ~in_1[2], ~in_1[3], in_1[4], ~in_1[5]);  // AND_Gate
  and Nfn (nfn_out, ~in_1[0], in_1[1], ~in_1[2], ~in_1[3], in_1[4], ~in_1[5]);  // AND_Gate
  and Halt (finaliza, in_1[0], in_1[1], ~in_1[2], ~in_1[3], in_1[4], ~in_1[5]);  // AND_Gate
  or or_1 (RegWrite, add_out, sub_out, mul_out, div_out, addi_out, and_out, or_out, xor_out, sll_out, srl_out, sra_out, MemRead, jal_pc, jalr_pc, nfn_out);
  or or_2 (ALUFont, MemRead, MemWrite, addi_out);
  and and_1 (and_1_out, ~blt_out, ~bne_out, beq_out);  // AND_Gate
  and and_2 (and_2_out, blt_out, ~bne_out, ~beq_out);  // AND_Gate
  and and_3 (and_3_out, ~blt_out, bne_out, ~beq_out);  // AND_Gate
  and and_4 (and_4_out, blt_out, ~bne_out, ~beq_out);  // AND_Gate
  or or_3 (Branch[0], and_1_out, and_2_out);
  or or_4 (Branch[1], and_3_out, and_4_out);
  or or_5 (Jump, jal_pc, jalr_pc);
  or or_6 (ALUop[0], sub_out, div_out, or_out, sll_out, sra_out);
  or or_7 (ALUop[1], mul_out, div_out, xor_out, sll_out);
  or or_8 (ALUop[2], and_out, or_out, xor_out, sll_out);
  or or_9 (ALUop[3], srl_out, sra_out);
  or or_10 (reg_ent, MemWrite, beq_out, bne_out, blt_out);

  assign MemtoReg = MemRead;

  // Other names for the same wires on the sheet: halt_out = finaliza; jal_out = jal_pc; jalr_out = jalr_pc;
  //   lw_out = MemRead; sw_out = MemWrite
endmodule

module branchs (
  input  [23:0] rs1,
  input  [23:0] rs2,
  input  [1:0] in_3,
  output out_4
);

  wire comparator_1_eq, comparator_2_eq, comparator_3_lt, not_1_out;
  wire [23:0] rs1_Beq, rs1_Blt, rs1_Bne, rs2_Beq, rs2_Blt, rs2_Bne;

  Demultiplexer #(.select(2), .width(24)) demultiplexer_1 (
    .out1(rs1_Beq), .out2(rs1_Bne), .out3(rs1_Blt), .in(rs1), .sel(in_3));  // open: out0
  Demultiplexer #(.select(2), .width(24)) demultiplexer_2 (
    .out1(rs2_Beq), .out2(rs2_Bne), .out3(rs2_Blt), .in(rs2), .sel(in_3));  // open: out0
  Comparator #(.width(24)) comparator_1 (.a(rs1_Beq), .b(rs2_Beq), .eq(comparator_1_eq));  // open: gt, lt
  Comparator #(.width(24)) comparator_2 (.a(rs1_Bne), .b(rs2_Bne), .eq(comparator_2_eq));  // open: gt, lt
  Comparator #(.width(24)) comparator_3 (.a(rs1_Blt), .b(rs2_Blt), .lt(comparator_3_lt));  // open: gt, eq
  not not_1 (not_1_out, comparator_2_eq);
  Multiplexer #(.select(2)) multiplexer_1 (
    .in0(1'b0), .in1(comparator_1_eq), .in2(not_1_out), .in3(comparator_3_lt), .out(out_4), .sel(in_3));

  // Other names for the same wires on the sheet: funct[1:0] = in_3
endmodule
