// Logisim project RiscV.circ as structural Verilog: 10 circuits, main circuit main
module main (
);

  wire ALUSrc_ID_EX, ALUSrc_IF_ID, ALUzero_ID_EX, and_1_out, Branch_ID_EX, Branch_IF_ID, clock_1_out,
       clock_2_out, funct7_ID_EX, MemRead_EX_MEM, MemRead_ID_EX, MemRead_IF_ID, MemtoReg_EX_MEM,
       MemtoReg_ID_EX, MemtoReg_IF_ID, MemtoReg_MEM_WB, MemWrite_EX_MEM, MemWrite_ID_EX, MemWrite_IF_ID,
       RegWrite_EX_MEM, RegWrite_ID_EX, RegWrite_IF_ID, RegWrite_MEM_WB;
  wire [1:0] ALUOp_ID_EX, ALUOp_IF_ID;
  wire [2:0] funct3_ID_EX;
  wire [3:0] ALUSel_ID_EX;
  wire [4:0] RD_EX_MEM, RD_ID_EX, RD_MEM_WB, RS1_EX_MEM, RS1_ID_EX, RS2_EX_MEM, RS2_ID_EX;
  wire [31:0] adder_1_out, adder_2_out, ALUout_EX_MEM, ALUout_ID_EX, ALUout_MEM_WB, Imm_ID_EX, Imm_IF_ID,
       Inst_in_IF_ID, instr_out_IF_ID, multiplexer_1_out, multiplexer_2_out, multiplexer_3_out, PC_in_IF_ID,
       PC_out_ID_EX, PC_out_IF_ID, ReadData1_ID_EX, ReadData1_IF_ID, ReadData2_ID_EX, ReadData2_IF_ID,
       ReadData_RAM_EX_MEM, ReadData_RAM_MEM_WB, WriteData_EX_MEM;

  Clock clock_1 (.out(clock_1_out));
  Register #(.width(32)) register_1 (
    .D(multiplexer_1_out), .en(clock_1_out), .clk(clock_1_out), .Q(PC_in_IF_ID));  // open: clr
  and and_1 (and_1_out, ALUzero_ID_EX, Branch_ID_EX);
  Multiplexer #(.width(32)) multiplexer_1 (
    .in0(adder_2_out), .in1(adder_1_out), .out(multiplexer_1_out), .sel(and_1_out));
  ROM #(.addrWidth(24), .dataWidth(32)) rom_1 (.addr(PC_in_IF_ID[23:0]), .data(Inst_in_IF_ID));
  Adder #(.width(32)) adder_1 (.a(PC_in_IF_ID), .b(Imm_ID_EX), .out(adder_1_out));  // open: cin, cout
  Adder #(.width(32)) adder_2 (.a(PC_in_IF_ID), .b(32'h4), .out(adder_2_out));  // open: cin, cout
  // Probe on adder_2_out
  // Probe on instr_out_IF_ID[11:7]
  // Probe on instr_out_IF_ID[24:20]
  // Probe on instr_out_IF_ID[19:15]
  // Probe on ReadData_RAM_MEM_WB
  // Probe on instr_out_IF_ID
  // Probe on ALUout_MEM_WB
  Multiplexer #(.width(32)) multiplexer_2 (
    .in0(ALUout_MEM_WB), .in1(ReadData_RAM_MEM_WB), .out(multiplexer_2_out), .sel(MemtoReg_MEM_WB));
  // Probe on RD_MEM_WB
  // Probe on Imm_IF_ID
  UNIDCtrl unidctrl_1 (
    .INSTRUCAO(instr_out_IF_ID), .out_2(MemWrite_IF_ID), .out_3(ALUSrc_IF_ID), .out_4(RegWrite_IF_ID),
    .out_5(MemtoReg_IF_ID), .out_6(MemRead_IF_ID), .out_7(Branch_IF_ID), .out_8(ALUOp_IF_ID));
  REG_IF_ID reg_if_id_1 (
    .PC_in(PC_in_IF_ID), .Inst_in(Inst_in_IF_ID), .stall(1'b0), .flush(1'b0), .PC_out(PC_out_IF_ID),
    .Inst_out(instr_out_IF_ID));
  // Probe on multiplexer_2_out
  ImediatoGenerator imediatogenerator_1 (.OPCODE(instr_out_IF_ID), .out_2(Imm_IF_ID));
  // Probe on ReadData1_IF_ID
  bancoRegistradores bancoregistradores_1 (
    .rsi2(instr_out_IF_ID[24:20]), .rdi(RD_MEM_WB), .data(multiplexer_2_out), .WE(RegWrite_MEM_WB),
    .rsi1(instr_out_IF_ID[19:15]), .rs1(ReadData1_IF_ID), .rs2(ReadData2_IF_ID));
  // Probe on MemWrite_IF_ID
  // Probe on ALUSrc_IF_ID
  // Probe on RegWrite_IF_ID
  // Probe on Branch_IF_ID
  // Probe on ALUOp_IF_ID
  // Probe on ReadData2_IF_ID
  // Probe on MemtoReg_IF_ID
  // Probe on MemRead_IF_ID
  // Probe on multiplexer_3_out
  Multiplexer #(.width(32)) multiplexer_3 (
    .in0(ReadData2_ID_EX), .in1(Imm_ID_EX), .out(multiplexer_3_out), .sel(ALUSrc_ID_EX));
  // Probe on ALUSel_ID_EX
  ULA ula_1 (
    .sel(ALUSel_ID_EX), .dataA(ReadData1_ID_EX), .dataB(multiplexer_3_out), .dataD(ALUout_ID_EX),
    .zero(ALUzero_ID_EX));
  ALUCtrl aluctrl_1 (.ALUop(ALUOp_ID_EX), .funct3_in(funct3_ID_EX), .funct7_5_in(funct7_ID_EX), .ALUsel(ALUSel_ID_EX));
  REG_ID_EX reg_id_ex_1 (
    .PC_in(PC_out_IF_ID), .ReadData1_in(ReadData1_IF_ID), .ReadData2_in(ReadData2_IF_ID), .Imm_in(Imm_IF_ID),
    .rs1_in(instr_out_IF_ID[19:15]), .rs2_in(instr_out_IF_ID[24:20]), .rd_in(instr_out_IF_ID[11:7]),
    .funct3_in(PC_out_IF_ID[14:12]), .funct7_5_in(PC_out_IF_ID[30]), .RegWrite_in(RegWrite_IF_ID),
    .MemToReg_in(MemtoReg_IF_ID), .MemRead_in(MemRead_IF_ID), .MemWrite_in(MemWrite_IF_ID),
    .ALUSrc_in(ALUSrc_IF_ID), .ALUOp_in(ALUOp_IF_ID), .Branch_in(Branch_IF_ID), .stall(1'b0), .flush(1'b0),
    .PC_out(PC_out_ID_EX), .ReadData1_out(ReadData1_ID_EX), .ReadData2_out(ReadData2_ID_EX),
    .Imm_out(Imm_ID_EX), .rs1_out(RS1_ID_EX), .rs2_out(RS2_ID_EX), .rd_out(RD_ID_EX),
    .funct3_out(funct3_ID_EX), .funct7_5_out(funct7_ID_EX), .RegWrite_out(RegWrite_ID_EX),
    .MemToReg_out(MemtoReg_ID_EX), .MemRead_out(MemRead_ID_EX), .MemWrite_out(MemWrite_ID_EX),
    .ALUSrc_out(ALUSrc_ID_EX), .ALUOp_out(ALUOp_ID_EX), .Branch_out(Branch_ID_EX));
  // Probe on ALUSel_ID_EX
  // Probe on ALUout_ID_EX
  Clock clock_2 (.out(clock_2_out));
  // Probe on ALUout_ID_EX
  // Probe on ReadData2_ID_EX[25:2]
  RAM #(.addrWidth(24), .dataWidth(32)) ram_1 (
    .addr(ReadData2_ID_EX[25:2]), .we(MemWrite_ID_EX), .oe(MemRead_ID_EX), .clk(clock_2_out),
    .din(ReadData2_ID_EX), .dout(ReadData_RAM_EX_MEM));
  // Probe on ALUout_EX_MEM
  REG_EX_MEM reg_ex_mem_1 (
    .ALUResult_in(ALUout_ID_EX), .WriteData_in(ReadData2_ID_EX), .rd_in(RD_ID_EX), .rs1_in(RS1_ID_EX),
    .rs2_in(RS2_ID_EX), .RegWrite_in(RegWrite_ID_EX), .MemToReg_in(MemtoReg_ID_EX),
    .MemRead_in(MemRead_ID_EX), .MemWrite_in(MemWrite_ID_EX), .ALUResult_out(ALUout_EX_MEM),
    .WriteData_out(WriteData_EX_MEM), .rd_out(RD_EX_MEM), .rs1_out(RS1_EX_MEM), .rs2_out(RS2_EX_MEM),
    .RegWrite_out(RegWrite_EX_MEM), .MemToReg_out(MemtoReg_EX_MEM), .MemRead_out(MemRead_EX_MEM),
    .MemWrite_out(MemWrite_EX_MEM));
  // Probe on ReadData_RAM_EX_MEM
  // Probe on ALUout_EX_MEM
  // Probe on ALUout_MEM_WB
  REG_MEM_WB reg_mem_wb_1 (
    .ReadData_in(ReadData_RAM_EX_MEM), .ALUResult_in(ALUout_EX_MEM), .rd_in(RD_EX_MEM),
    .RegWrite_in(RegWrite_EX_MEM), .MemToReg_in(MemtoReg_EX_MEM), .ReadData_out(ReadData_RAM_MEM_WB),
    .ALUResult_out(ALUout_MEM_WB), .rd_out(RD_MEM_WB), .RegWrite_out(RegWrite_MEM_WB),
    .MemToReg_out(MemtoReg_MEM_WB));

  // Other names for the same wires on the sheet: RD_IF_ID[4:0] = instr_out_IF_ID[11:7];
  //   RS1_IF_ID[4:0] = instr_out_IF_ID[19:15]; RS2_IF_ID[4:0] = instr_out_IF_ID[24:20]

  // Notes on the sheet:
  //   contents of rom_1 (hex, n*v repeats v):
  //   600513 0 0 0 300c93 0 0 0 41950cb3 0 0 0 ff9506e3
  //   endereco
endmodule

module bancoRegistradores (
  input  [4:0] rsi1,
  input  [4:0] rsi2,
  input  [4:0] rdi,
  input  [31:0] data,
  input  WE,
  output [31:0] rs1,
  output [31:0] rs2
);

  wire clk_t, x0we_t, x1we_t, x2we_t, x3we_t, x4we_t, x5we_t, x6we_t, x7we_t, x8we_t, x9we_t, x10we_t,
       x11we_t, x12we_t, x13we_t, x14we_t, x15we_t, x16we_t, x17we_t, x18we_t, x19we_t, x20we_t, x21we_t,
       x22we_t, x23we_t, x24we_t, x25we_t, x26we_t, x27we_t, x28we_t, x29we_t, x30we_t, x31we_t;
  wire [31:0] x1q_t, x2q_t, x3q_t, x4q_t, x5q_t, x6q_t, x7q_t, x8q_t, x9q_t, x10q_t, x11q_t, x12q_t, x13q_t,
       x14q_t, x15q_t, x16q_t, x17q_t, x18q_t, x19q_t, x20q_t, x21q_t, x22q_t, x23q_t, x24q_t, x25q_t,
       x26q_t, x27q_t, x28q_t, x29q_t, x30q_t, x31q_t;

  // Probe on data
  Clock clock_1 (.out(clk_t));
  Demultiplexer #(.select(5)) demultiplexer_1 (
    .out0(x0we_t), .out1(x1we_t), .out2(x2we_t), .out3(x3we_t), .out4(x4we_t), .out5(x5we_t), .out6(x6we_t),
    .out7(x7we_t), .out8(x8we_t), .out9(x9we_t), .out10(x10we_t), .out11(x11we_t), .out12(x12we_t),
    .out13(x13we_t), .out14(x14we_t), .out15(x15we_t), .out16(x16we_t), .out17(x17we_t), .out18(x18we_t),
    .out19(x19we_t), .out20(x20we_t), .out21(x21we_t), .out22(x22we_t), .out23(x23we_t), .out24(x24we_t),
    .out25(x25we_t), .out26(x26we_t), .out27(x27we_t), .out28(x28we_t), .out29(x29we_t), .out30(x30we_t),
    .out31(x31we_t), .in(WE), .sel(rdi));
  Register #(.width(32)) x4 (.D(data), .en(x4we_t), .clk(clk_t), .Q(x4q_t));  // open: clr
  Register #(.width(32)) x8 (.D(data), .en(x8we_t), .clk(clk_t), .Q(x8q_t));  // open: clr
  Register #(.width(32)) x12 (.D(data), .en(x12we_t), .clk(clk_t), .Q(x12q_t));  // open: clr
  Register #(.width(32)) x16 (.D(data), .en(x16we_t), .clk(clk_t), .Q(x16q_t));  // open: clr
  Register #(.width(32)) x20 (.D(data), .en(x20we_t), .clk(clk_t), .Q(x20q_t));  // open: clr
  Register #(.width(32)) x24 (.D(data), .en(x24we_t), .clk(clk_t), .Q(x24q_t));  // open: clr
  Register #(.width(32)) x28 (.D(data), .en(x28we_t), .clk(clk_t), .Q(x28q_t));  // open: clr
  Register #(.width(32)) x1 (.D(data), .en(x1we_t), .clk(clk_t), .Q(x1q_t));  // open: clr
  Register #(.width(32)) x5 (.D(data), .en(x5we_t), .clk(clk_t), .Q(x5q_t));  // open: clr
  Register #(.width(32)) x9 (.D(data), .en(x9we_t), .clk(clk_t), .Q(x9q_t));  // open: clr
  Register #(.width(32)) x13 (.D(data), .en(x13we_t), .clk(clk_t), .Q(x13q_t));  // open: clr
  Register #(.width(32)) x17 (.D(data), .en(x17we_t), .clk(clk_t), .Q(x17q_t));  // open: clr
  Register #(.width(32)) x21 (.D(data), .en(x21we_t), .clk(clk_t), .Q(x21q_t));  // open: clr
  Register #(.width(32)) x25 (.D(data), .en(x25we_t), .clk(clk_t), .Q(x25q_t));  // open: clr
  Register #(.width(32)) x29 (.D(data), .en(x29we_t), .clk(clk_t), .Q(x29q_t));  // open: clr
  Register #(.width(32)) x2 (.D(data), .en(x2we_t), .clk(clk_t), .Q(x2q_t));  // open: clr
  Register #(.width(32)) x6 (.D(data), .en(x6we_t), .clk(clk_t), .Q(x6q_t));  // open: clr
  Register #(.width(32)) x10 (.D(data), .en(x10we_t), .clk(clk_t), .Q(x10q_t));  // open: clr
  Register #(.width(32)) x14 (.D(data), .en(x14we_t), .clk(clk_t), .Q(x14q_t));  // open: clr
  Register #(.width(32)) x18 (.D(data), .en(x18we_t), .clk(clk_t), .Q(x18q_t));  // open: clr
  Register #(.width(32)) x22 (.D(data), .en(x22we_t), .clk(clk_t), .Q(x22q_t));  // open: clr
  Register #(.width(32)) x26 (.D(data), .en(x26we_t), .clk(clk_t), .Q(x26q_t));  // open: clr
  Register #(.width(32)) x30 (.D(data), .en(x30we_t), .clk(clk_t), .Q(x30q_t));  // open: clr
  Register #(.width(32)) x3 (.D(data), .en(x3we_t), .clk(clk_t), .Q(x3q_t));  // open: clr
  Register #(.width(32)) x7 (.D(data), .en(x7we_t), .clk(clk_t), .Q(x7q_t));  // open: clr
  Register #(.width(32)) x11 (.D(data), .en(x11we_t), .clk(clk_t), .Q(x11q_t));  // open: clr
  Register #(.width(32)) x15 (.D(data), .en(x15we_t), .clk(clk_t), .Q(x15q_t));  // open: clr
  Register #(.width(32)) x19 (.D(data), .en(x19we_t), .clk(clk_t), .Q(x19q_t));  // open: clr
  Register #(.width(32)) x23 (.D(data), .en(x23we_t), .clk(clk_t), .Q(x23q_t));  // open: clr
  Register #(.width(32)) x27 (.D(data), .en(x27we_t), .clk(clk_t), .Q(x27q_t));  // open: clr
  Register #(.width(32)) x31 (.D(data), .en(x31we_t), .clk(clk_t), .Q(x31q_t));  // open: clr
  Multiplexer #(.select(5), .width(32)) multiplexer_1 (
    .in0({32{1'b0}}), .in1(x1q_t), .in2(x2q_t), .in3(x3q_t), .in4(x4q_t), .in5(x5q_t), .in6(x6q_t),
    .in7(x7q_t), .in8(x8q_t), .in9(x9q_t), .in10(x10q_t), .in11(x11q_t), .in12(x12q_t), .in13(x13q_t),
    .in14(x14q_t), .in15(x15q_t), .in16(x16q_t), .in17(x17q_t), .in18(x18q_t), .in19(x19q_t), .in20(x20q_t),
    .in21(x21q_t), .in22(x22q_t), .in23(x23q_t), .in24(x24q_t), .in25(x25q_t), .in26(x26q_t), .in27(x27q_t),
    .in28(x28q_t), .in29(x29q_t), .in30(x30q_t), .in31(x31q_t), .out(rs1), .sel(rsi1));
  Multiplexer #(.select(5), .width(32)) multiplexer_2 (
    .in0({32{1'b0}}), .in1(x1q_t), .in2(x2q_t), .in3(x3q_t), .in4(x4q_t), .in5(x5q_t), .in6(x6q_t),
    .in7(x7q_t), .in8(x8q_t), .in9(x9q_t), .in10(x10q_t), .in11(x11q_t), .in12(x12q_t), .in13(x13q_t),
    .in14(x14q_t), .in15(x15q_t), .in16(x16q_t), .in17(x17q_t), .in18(x18q_t), .in19(x19q_t), .in20(x20q_t),
    .in21(x21q_t), .in22(x22q_t), .in23(x23q_t), .in24(x24q_t), .in25(x25q_t), .in26(x26q_t), .in27(x27q_t),
    .in28(x28q_t), .in29(x29q_t), .in30(x30q_t), .in31(x31q_t), .out(rs2), .sel(rsi2));

  // Other names for the same wires on the sheet: rd_t[31:0] = data; rdi_t[4:0] = rdi; rs1_t[31:0] = rs1;
  //   rs2_t[31:0] = rs2; rsi1_t[4:0] = rsi1; rsi2_t[4:0] = rsi2; we_t = WE
endmodule

module ULA (
  input  [31:0] dataA,
  input  [31:0] dataB,
  input  [3:0] sel,
  output [31:0] dataD,
  output zero
);

  wire [31:0] adder_1_out, and_1_out, or_1_out, shifter_1_out, subtractor_1_out;

  // Probe on and_1_out
  assign and_1_out = dataA & dataB;  // AND_Gate and_1, 32 bits wide
  // Probe on or_1_out
  assign or_1_out = dataA | dataB;  // OR_Gate or_1, 32 bits wide
  // Probe on adder_1_out
  Adder #(.width(32)) adder_1 (.a(dataA), .b(dataB), .out(adder_1_out));  // open: cin, cout
  // Probe on shifter_1_out
  Shifter #(.width(32)) shifter_1 (.in(dataA), .\dist (dataB[4:0]), .out(shifter_1_out));
  Subtractor #(.width(32)) subtractor_1 (.a(dataA), .b(dataB), .out(subtractor_1_out));  // open: bin, bout
  // Probe on subtractor_1_out
  Multiplexer #(.select(4), .width(32)) multiplexer_1 (
    .in0(and_1_out), .in1(or_1_out), .in2(adder_1_out), .in3(shifter_1_out), .in4(dataB), .in5(dataB),
    .in6(subtractor_1_out), .in7(dataB), .in8(dataB), .in9(dataB), .in10(dataB), .in11(dataB), .in12(dataB),
    .in13(dataB), .in14(dataB), .in15(dataB), .out(dataD), .sel(sel));
  nor nor_1 (zero, dataD[0], dataD[1], dataD[2], dataD[3], dataD[4], dataD[5], dataD[6], dataD[7], dataD[8], dataD[9], dataD[10], dataD[11], dataD[12], dataD[13], dataD[14], dataD[15], dataD[16], dataD[17], dataD[18], dataD[19], dataD[20], dataD[21], dataD[22], dataD[23], dataD[24], dataD[25], dataD[26], dataD[27], dataD[28], dataD[29], dataD[30], dataD[31]);

  // Other names for the same wires on the sheet: dataA_t[31:0] = dataA; dataB_t[31:0] = dataB; dataD_t[31:0] = dataD;
  //   sel_t[3:0] = sel

  // Notes on the sheet:
  //   desloca no maximo 2 elevado a 5 menos 1
  //   0000 and
  //   0001 or
  //   0010 add
  //   0110 sub
  //   0011 sll
  //   depois implementos o restante
endmodule

module ImediatoGenerator (
  input  [31:0] OPCODE,
  output [31:0] out_2
);

  wire and_1_out, and_2_out, and_3_out, and_5_out, and_6_out, S0, S1, S2;
  wire [31:0] bit_extender_1_out, bit_extender_2_out, bit_extender_3_out, bit_extender_4_out;

  // Probe on OPCODE[6:0]
  and and_1 (and_1_out, OPCODE[0], OPCODE[1], OPCODE[2], ~OPCODE[4], OPCODE[5], OPCODE[6]);  // AND_Gate
  and and_2 (and_2_out, OPCODE[0], OPCODE[1], ~OPCODE[2], ~OPCODE[3], OPCODE[5], OPCODE[6]);  // AND_Gate
  and and_3 (and_3_out, OPCODE[0], OPCODE[1], ~OPCODE[2], ~OPCODE[3], ~OPCODE[5], ~OPCODE[6]);  // AND_Gate
  and and_4 (S1, OPCODE[0], OPCODE[1], ~OPCODE[2], ~OPCODE[4], ~OPCODE[3], OPCODE[5]);  // AND_Gate
  and and_5 (and_5_out, OPCODE[0], OPCODE[1], OPCODE[2], OPCODE[3], ~OPCODE[4], OPCODE[5], OPCODE[6]);  // AND_Gate
  and and_6 (and_6_out, OPCODE[0], OPCODE[1], OPCODE[2], ~OPCODE[3], OPCODE[4], OPCODE[5], ~OPCODE[6]);  // AND_Gate
  or or_1 (S2, and_1_out, and_2_out, and_3_out);
  or or_2 (S0, and_5_out, and_6_out);
  // Probe on {S0, S1, S2}
  assign bit_extender_1_out = {{20{OPCODE[31]}}, OPCODE[31:20]};  // Bit_Extender bit_extender_1
  // Probe on bit_extender_1_out
  assign bit_extender_2_out = {{20{OPCODE[31]}}, {OPCODE[31:25], OPCODE[11:7]}};  // Bit_Extender bit_extender_2
  assign bit_extender_3_out = {{19{OPCODE[31]}}, {OPCODE[31], OPCODE[7], OPCODE[30:25], OPCODE[11:8], 1'b0}};  // Bit_Extender bit_extender_3
  // Probe on bit_extender_3_out
  // Probe on {OPCODE[31:12], {12{1'b0}}}
  // Probe on bit_extender_2_out
  // Probe on {OPCODE[31], OPCODE[19:12], OPCODE[20], OPCODE[30:21], 1'b0}
  assign bit_extender_4_out = {{11{OPCODE[31]}}, {OPCODE[31], OPCODE[19:12], OPCODE[20], OPCODE[30:21], 1'b0}};  // Bit_Extender bit_extender_4
  Multiplexer #(.select(3), .width(32)) multiplexer_1 (
    .in1(bit_extender_1_out), .in2(bit_extender_2_out), .in3(bit_extender_3_out),
    .in4({OPCODE[31:12], {12{1'b0}}}), .in5(bit_extender_4_out), .out(out_2), .sel({S0, S1, S2}));  // open: in0, in6, in7
  // Probe on out_2

  // Other names for the same wires on the sheet: A = OPCODE[0]; B = OPCODE[1]; C = OPCODE[2]; D = OPCODE[3];
  //   E = OPCODE[4]; F = OPCODE[5]; G = OPCODE[6]; seletor[2:0] = {S0, S1, S2}

  // Notes on the sheet:
  //   OPCODE: initial=0x7a17d
  //   separa os bits em um circ combinacional e gera 3 bits de controle para o mux dependendo do OPCODE
  //   tipo S
  //   tipo U
  //   tipo J
  //   tipo I
  //   tipo B
endmodule

module ALUCtrl (
  input  [1:0] ALUop,
  input  [2:0] funct3_in,
  input  funct7_5_in,
  output [3:0] ALUsel
);

  wire and_1_out, and_2_out, and_3_out, or_1_out;

  and and_1 (and_1_out, funct3_in[2], funct3_in[1], ~funct3_in[0]);  // AND_Gate
  and and_2 (and_2_out, ~funct3_in[2], ~funct3_in[1], funct3_in[0]);  // AND_Gate
  and and_3 (and_3_out, ALUop[1], funct7_5_in, ~funct3_in[2], ~funct3_in[1], ~funct3_in[0]);  // AND_Gate
  or or_1 (or_1_out, and_1_out, and_2_out);
  or or_2 (ALUsel[1], ~ALUop[1], ALUop[0], ~funct3_in[2], ~funct3_in[1]);  // OR_Gate
  or or_3 (ALUsel[2], ALUop[0], and_3_out);
  // NoConnect on nothing
  and and_4 (ALUsel[0], ALUop[1], ~ALUop[0], or_1_out);  // AND_Gate

  assign ALUsel[3] = 1'b0;

  // Other names for the same wires on the sheet: A0 = ALUop[0]; A1 = ALUop[1]; F7 = funct7_5_in; F0 = funct3_in[0];
  //   F1 = funct3_in[1]; F2 = funct3_in[2]

  // Notes on the sheet:
  //   ALUop
  //   funct3
  //   funct7
  //   A1 · ~A0 · ( (F2 · F1 · ~F0) + (~F2 · ~F1 · F0) )
  //   (~A1 + A0 + ~F2 + ~F1)
  //   A0 + (A1 · F7 · ~F2 · ~F1 · ~F0)
endmodule

module UNIDCtrl (
  input  [31:0] INSTRUCAO,
  output out_2,
  output out_3,
  output out_4,
  output out_5,
  output out_6,
  output out_7,
  output [1:0] out_8
);

  wire and_2_out, not_1_out, or_3_out;
  wire [1:0] and_5_out;
  wire [4:0] and_1_out;

  and and_1 (and_1_out[0], ~INSTRUCAO[4], INSTRUCAO[5], ~INSTRUCAO[6]);  // AND_Gate
  and and_2 (and_2_out, ~INSTRUCAO[5], ~INSTRUCAO[6]);  // AND_Gate
  and and_3 (and_1_out[4], ~INSTRUCAO[4], ~INSTRUCAO[5], ~INSTRUCAO[6]);  // AND_Gate
  and and_4 (and_5_out[1], INSTRUCAO[4], INSTRUCAO[5], ~INSTRUCAO[6]);  // AND_Gate
  and and_5 (and_5_out[0], ~INSTRUCAO[4], INSTRUCAO[5], INSTRUCAO[6]);  // AND_Gate
  or or_1 (and_1_out[1], and_1_out[0], and_2_out);
  or or_2 (and_1_out[2], and_2_out, and_5_out[1]);
  or or_3 (or_3_out, INSTRUCAO[0], INSTRUCAO[1], INSTRUCAO[2], INSTRUCAO[3], INSTRUCAO[4], INSTRUCAO[5], INSTRUCAO[6], INSTRUCAO[7], INSTRUCAO[8], INSTRUCAO[9], INSTRUCAO[10], INSTRUCAO[11], INSTRUCAO[12], INSTRUCAO[13], INSTRUCAO[14], INSTRUCAO[15], INSTRUCAO[16], INSTRUCAO[17], INSTRUCAO[18], INSTRUCAO[19], INSTRUCAO[20], INSTRUCAO[21], INSTRUCAO[22], INSTRUCAO[23], INSTRUCAO[24], INSTRUCAO[25], INSTRUCAO[26], INSTRUCAO[27], INSTRUCAO[28], INSTRUCAO[29], INSTRUCAO[30], INSTRUCAO[31]);
  not not_1 (not_1_out, or_3_out);
  Multiplexer #(.width(8)) multiplexer_1 (
    .in0({and_5_out, and_5_out[0], {2{and_1_out[4]}}, and_1_out[2:0]}), .in1({8{1'b0}}),
    .out({out_8, out_7, out_6, out_5, out_4, out_3, out_2}), .sel(not_1_out));

  // Other names for the same wires on the sheet: op_4 = INSTRUCAO[4]; op_5 = INSTRUCAO[5]; op_6 = INSTRUCAO[6]

  // Notes on the sheet:
  //   Coloquei esse or por 
endmodule

module REG_IF_ID (
  input  [31:0] PC_in,
  input  [31:0] Inst_in,
  input  stall,
  input  flush,
  output [31:0] PC_out,
  output [31:0] Inst_out
);

  wire clock_1_out, clock_2_out, stall_t;
  wire [31:0] multiplexer_1_out, multiplexer_2_out;

  not not_1 (stall_t, stall);
  Multiplexer #(.width(32)) multiplexer_1 (.in0(PC_in), .in1({32{1'b0}}), .out(multiplexer_1_out), .sel(flush));
  Multiplexer #(.width(32)) multiplexer_2 (.in0(Inst_in), .in1({32{1'b0}}), .out(multiplexer_2_out), .sel(flush));
  Register #(.width(32)) register_1 (.D(multiplexer_1_out), .en(stall_t), .clk(clock_1_out), .Q(PC_out));  // open: clr
  Clock clock_1 (.out(clock_1_out));
  Register #(.width(32)) register_2 (
    .D(multiplexer_2_out), .en(stall_t), .clk(clock_2_out), .Q(Inst_out));  // open: clr
  Clock clock_2 (.out(clock_2_out));

  // Other names for the same wires on the sheet: flush_t = flush

  // Notes on the sheet:
  //   Valor atual do PC
  //   Instrução buscada da memória (ROM) 
  //   manter valores anteriores se  1
endmodule

module REG_ID_EX (
  input  [31:0] PC_in,
  input  [31:0] ReadData1_in,
  input  [31:0] ReadData2_in,
  input  [31:0] Imm_in,
  input  [4:0] rs1_in,
  input  [4:0] rs2_in,
  input  [4:0] rd_in,
  input  [2:0] funct3_in,
  input  funct7_5_in,
  input  RegWrite_in,
  input  MemToReg_in,
  input  MemRead_in,
  input  MemWrite_in,
  input  ALUSrc_in,
  input  [1:0] ALUOp_in,
  input  Branch_in,
  input  stall,
  input  flush,
  output [31:0] PC_out,
  output [31:0] ReadData1_out,
  output [31:0] ReadData2_out,
  output [31:0] Imm_out,
  output [4:0] rs1_out,
  output [4:0] rs2_out,
  output [4:0] rd_out,
  output [2:0] funct3_out,
  output funct7_5_out,
  output RegWrite_out,
  output MemToReg_out,
  output MemRead_out,
  output MemWrite_out,
  output ALUSrc_out,
  output [1:0] ALUOp_out,
  output Branch_out
);

  wire clock_1_out, clock_2_out, clock_3_out, clock_4_out, clock_5_out, clock_6_out, clock_7_out,
       clock_8_out, clock_9_out, stall_t;
  wire [3:0] multiplexer_7_out;
  wire [4:0] multiplexer_4_out, multiplexer_5_out, multiplexer_6_out;
  wire [7:0] multiplexer_8_out;
  wire [31:0] multiplexer_1_out, multiplexer_2_out, multiplexer_3_out, multiplexer_9_out;

  not not_1 (stall_t, stall);
  Multiplexer #(.width(32)) multiplexer_1 (.in0(ReadData1_in), .in1({32{1'b0}}), .out(multiplexer_1_out), .sel(flush));
  Multiplexer #(.width(32)) multiplexer_2 (.in0(ReadData2_in), .in1({32{1'b0}}), .out(multiplexer_2_out), .sel(flush));
  Multiplexer #(.width(32)) multiplexer_3 (.in0(Imm_in), .in1({32{1'b0}}), .out(multiplexer_3_out), .sel(flush));
  Multiplexer #(.width(5)) multiplexer_4 (.in0(rs1_in), .in1({5{1'b0}}), .out(multiplexer_4_out), .sel(flush));
  Multiplexer #(.width(5)) multiplexer_5 (.in0(rs2_in), .in1({5{1'b0}}), .out(multiplexer_5_out), .sel(flush));
  Multiplexer #(.width(5)) multiplexer_6 (.in0(rd_in), .in1({5{1'b0}}), .out(multiplexer_6_out), .sel(flush));
  Multiplexer #(.width(4)) multiplexer_7 (
    .in0({funct7_5_in, funct3_in}), .in1(4'b0000), .out(multiplexer_7_out), .sel(flush));
  Multiplexer #(.width(8)) multiplexer_8 (
    .in0({Branch_in, ALUOp_in, ALUSrc_in, MemWrite_in, MemRead_in, MemToReg_in, RegWrite_in}),
    .in1({8{1'b0}}), .out(multiplexer_8_out), .sel(flush));
  Multiplexer #(.width(32)) multiplexer_9 (.in0(PC_in), .in1({32{1'b0}}), .out(multiplexer_9_out), .sel(flush));
  Clock clock_1 (.out(clock_1_out));
  Clock clock_2 (.out(clock_2_out));
  Clock clock_3 (.out(clock_3_out));
  Clock clock_4 (.out(clock_4_out));
  Clock clock_5 (.out(clock_5_out));
  Clock clock_6 (.out(clock_6_out));
  Register #(.width(4)) register_1 (
    .D(multiplexer_7_out), .en(stall_t), .clk(clock_7_out), .Q({funct7_5_out, funct3_out}));  // open: clr
  Clock clock_7 (.out(clock_7_out));
  Register register_2 (
    .D(multiplexer_8_out), .en(stall_t), .clk(clock_8_out),
    .Q({Branch_out, ALUOp_out, ALUSrc_out, MemWrite_out, MemRead_out, MemToReg_out, RegWrite_out}));  // open: clr
  Clock clock_8 (.out(clock_8_out));
  Register #(.width(32)) register_3 (.D(multiplexer_9_out), .en(stall_t), .clk(clock_9_out), .Q(PC_out));  // open: clr
  Clock clock_9 (.out(clock_9_out));
  Register #(.width(32)) register_4 (
    .D(multiplexer_1_out), .en(stall_t), .clk(clock_1_out), .Q(ReadData1_out));  // open: clr
  Register #(.width(32)) register_5 (
    .D(multiplexer_2_out), .en(stall_t), .clk(clock_2_out), .Q(ReadData2_out));  // open: clr
  Register #(.width(32)) register_6 (.D(multiplexer_3_out), .en(stall_t), .clk(clock_3_out), .Q(Imm_out));  // open: clr
  Register #(.width(5)) register_7 (.D(multiplexer_4_out), .en(stall_t), .clk(clock_4_out), .Q(rs1_out));  // open: clr
  Register #(.width(5)) register_8 (.D(multiplexer_5_out), .en(stall_t), .clk(clock_5_out), .Q(rs2_out));  // open: clr
  Register #(.width(5)) register_9 (.D(multiplexer_6_out), .en(stall_t), .clk(clock_6_out), .Q(rd_out));  // open: clr

  // Other names for the same wires on the sheet: flush_t = flush

  // Notes on the sheet:
  //   PC vindo do REG_IF_ID 
  //   Saída do banco de registradores (rs1)
  //   Saída do banco de registradores (rs2)
  //   Saída do gerador de imediato
  //   Campo rs2 da instru
  //   Campo RD da instru
  //   Bits 14:12 da instru
  //   Bit 30 (funct7[5])
  //   Campo rs1 da instru
  //   Bits da unidade de controle, juntei os bits, salvei e separei pra nao ocupar tanto espaco com registradores
endmodule

module REG_EX_MEM (
  input  [31:0] ALUResult_in,
  input  [31:0] WriteData_in,
  input  [4:0] rd_in,
  input  [4:0] rs1_in,
  input  [4:0] rs2_in,
  input  RegWrite_in,
  input  MemToReg_in,
  input  MemRead_in,
  input  MemWrite_in,
  output [31:0] ALUResult_out,
  output [31:0] WriteData_out,
  output [4:0] rd_out,
  output [4:0] rs1_out,
  output [4:0] rs2_out,
  output RegWrite_out,
  output MemToReg_out,
  output MemRead_out,
  output MemWrite_out
);

  wire clock_1_out, clock_2_out, clock_3_out, clock_4_out, clock_5_out, clock_6_out, clock_7_out,
       clock_8_out, clock_9_out;

  Clock clock_1 (.out(clock_1_out));
  Clock clock_2 (.out(clock_2_out));
  Clock clock_3 (.out(clock_3_out));
  Clock clock_4 (.out(clock_4_out));
  Clock clock_5 (.out(clock_5_out));
  Clock clock_6 (.out(clock_6_out));
  Clock clock_7 (.out(clock_7_out));
  Clock clock_8 (.out(clock_8_out));
  Clock clock_9 (.out(clock_9_out));
  Register #(.width(32)) register_1 (
    .D(ALUResult_in), .en(clock_1_out), .clk(clock_1_out), .Q(ALUResult_out));  // open: clr
  Register #(.width(32)) register_2 (
    .D(WriteData_in), .en(clock_2_out), .clk(clock_2_out), .Q(WriteData_out));  // open: clr
  Register #(.width(5)) register_3 (.D(rd_in), .en(clock_3_out), .clk(clock_3_out), .Q(rd_out));  // open: clr
  Register #(.width(5)) register_4 (.D(rs1_in), .en(clock_4_out), .clk(clock_4_out), .Q(rs1_out));  // open: clr
  Register #(.width(5)) register_5 (.D(rs2_in), .en(clock_5_out), .clk(clock_5_out), .Q(rs2_out));  // open: clr
  Register #(.width(1)) register_6 (
    .D(RegWrite_in), .en(clock_6_out), .clk(clock_6_out), .Q(RegWrite_out));  // open: clr
  Register #(.width(1)) register_7 (
    .D(MemToReg_in), .en(clock_7_out), .clk(clock_7_out), .Q(MemToReg_out));  // open: clr
  Register #(.width(1)) register_8 (.D(MemRead_in), .en(clock_8_out), .clk(clock_8_out), .Q(MemRead_out));  // open: clr
  Register #(.width(1)) register_9 (
    .D(MemWrite_in), .en(clock_9_out), .clk(clock_9_out), .Q(MemWrite_out));  // open: clr

  // Notes on the sheet:
  //   Resultado da ALU no estagio EX
  //   Dado vindo de rs2, que sera escrito na memoria se for uma instrucao
  //   Usado no estagio WB para saber onde escrever o valor
  //   Diz se a instrucao atual deve escrever em um registrador
  //   Se 1, dado sera escrito ira vir da RAM
  //   Se 0, vira da ALU
  //   Ativa leitura da memoria
  //   Ativa escrita na memoria
endmodule

module REG_MEM_WB (
  input  [31:0] ReadData_in,
  input  [31:0] ALUResult_in,
  input  [4:0] rd_in,
  input  RegWrite_in,
  input  MemToReg_in,
  output [31:0] ReadData_out,
  output [31:0] ALUResult_out,
  output [4:0] rd_out,
  output RegWrite_out,
  output MemToReg_out
);

  wire clock_1_out, clock_2_out, clock_3_out, clock_4_out, clock_5_out;

  Clock clock_1 (.out(clock_1_out));
  Clock clock_2 (.out(clock_2_out));
  Clock clock_3 (.out(clock_3_out));
  Clock clock_4 (.out(clock_4_out));
  Clock clock_5 (.out(clock_5_out));
  Register #(.width(32)) register_1 (
    .D(ReadData_in), .en(clock_1_out), .clk(clock_1_out), .Q(ReadData_out));  // open: clr
  Register #(.width(32)) register_2 (
    .D(ALUResult_in), .en(clock_2_out), .clk(clock_2_out), .Q(ALUResult_out));  // open: clr
  Register #(.width(5)) register_3 (.D(rd_in), .en(clock_3_out), .clk(clock_3_out), .Q(rd_out));  // open: clr
  Register #(.width(1)) register_4 (
    .D(RegWrite_in), .en(clock_4_out), .clk(clock_4_out), .Q(RegWrite_out));  // open: clr
  Register #(.width(1)) register_5 (
    .D(MemToReg_in), .en(clock_5_out), .clk(clock_5_out), .Q(MemToReg_out));  // open: clr

  // Notes on the sheet:
  //   Usado quando intrucao e um load
  //   Usado quando a intrucao e do tipo aritmetica
  //   Serve para indicar onde escrever no banco de registradores
  //   Ativa escrita no banco de registradores
  //   Seleciona o dado a ser escrito no banco de registradores
endmodule
